// Logisim project md2.circ as structural Verilog: 1 circuit, main circuit main
module main (
);

  wire clock_1_out, comparator_1_gt, counter_1_carry, not_1_out, not_2_out, not_3_out, pull_resistor_1_node,
       pull_resistor_3_node, s_r_ff_1_q, s_r_ff_3_qn, subtractor_2_bout;
  wire [3:0] bit_extender_1_out, pull_resistor_5_node, pull_resistor_6_node, subtractor_1_out;
  wire [4:0] bit_extender_2_out, bit_extender_3_out, bit_extender_5_out, counter_1_q, transistor_1_out;
  wire [7:0] bit_extender_4_out;
  wire [23:0] pull_resistor_4_node, subtractor_2_out, transistor_4_out;

  Clock clock_1 (.out(clock_1_out));
  Pull_Resistor pull_resistor_1 (.node(pull_resistor_1_node));
  S_R_Flip_Flop s_r_ff_1 (
    .S(pull_resistor_1_node), .R(s_r_ff_1_q), .clk(clock_1_out), .Q(s_r_ff_1_q));  // open: reset, Qn, preset
  S_R_Flip_Flop s_r_ff_2 (.clk(clock_1_out));  // open: S, R, Q, reset, Qn, preset
  Pull_Resistor #(.pull(1)) pull_resistor_2 (.node(s_r_ff_1_q));
  Counter #(.max('h1f), .ongoal("stay"), .width(5)) counter_1 (
    .clr(s_r_ff_1_q), .up(pull_resistor_3_node), .count(pull_resistor_3_node), .clk(clock_1_out),
    .carry(counter_1_carry), .Q(counter_1_q));  // open: load, D
  Pull_Resistor #(.pull(1)) pull_resistor_3 (.node(pull_resistor_3_node));
  Pull_Resistor pull_resistor_4 (.node(pull_resistor_4_node));
  // Probe on bit_extender_1_out
  Bit_Extender #(.in_width(24), .out_width(4), .\type ("zero")) bit_extender_1 (
    .in(pull_resistor_4_node), .out(bit_extender_1_out));
  Pull_Resistor pull_resistor_5 (.node(pull_resistor_5_node));
  not not_1 (not_1_out, counter_1_carry);
  // Probe on subtractor_1_out
  Subtractor #(.width(4)) subtractor_1 (
    .a(pull_resistor_5_node), .b(bit_extender_1_out), .out(subtractor_1_out));  // open: bin, bout
  assign bit_extender_2_out = {{1{1'b0}}, subtractor_1_out};  // Bit_Extender bit_extender_2
  assign bit_extender_3_out = {{1{1'b1}}, subtractor_1_out};  // Bit_Extender bit_extender_3
  Comparator #(.mode("unsigned"), .width(5)) comparator_1 (
    .a(bit_extender_2_out), .b(counter_1_q), .gt(comparator_1_gt));  // open: eq, lt
  not not_2 (not_2_out, counter_1_carry);
  not not_3 (not_3_out, comparator_1_gt);
  Transistor #(.width(5)) transistor_1 (.in(counter_1_q), .out(transistor_1_out), .gate(counter_1_carry));
  Pull_Resistor pull_resistor_6 (.node(pull_resistor_6_node));
  Transistor #(.width(4)) transistor_2 (.in(subtractor_1_out), .out(pull_resistor_6_node), .gate(not_3_out));
  assign bit_extender_4_out = {{4{1'b0}}, pull_resistor_6_node};  // Bit_Extender bit_extender_4
  S_R_Flip_Flop s_r_ff_3 (.clk(clock_1_out), .Qn(s_r_ff_3_qn), .preset(clock_1_out));  // open: S, R, Q, reset
  RAM #(.addrWidth(5)) Padding (
    .addr(transistor_1_out), .we(not_1_out), .oe(counter_1_carry), .clk(clock_1_out), .din(bit_extender_4_out));  // open: dout
  Transistor #(.width(5)) transistor_3 (.in(bit_extender_5_out), .out(transistor_1_out), .gate(not_2_out));
  Pull_Resistor pull_resistor_7 (.node(transistor_1_out));
  Register #(.width(24)) Length (
    .D(24'h100012), .en(s_r_ff_3_qn), .clk(clock_1_out), .Q(pull_resistor_4_node));  // open: clr
  Pull_Resistor #(.pull(1)) pull_resistor_8 (.node(s_r_ff_3_qn));
  Bit_Extender #(.in_width(24), .out_width(5), .\type ("zero")) bit_extender_5 (
    .in(subtractor_2_out), .out(bit_extender_5_out));
  Subtractor #(.width(24)) subtractor_2 (
    .a({24{1'b1}}), .b(pull_resistor_4_node), .out(subtractor_2_out), .bout(subtractor_2_bout));  // open: bin
  RAM #(.addrWidth(24)) Data (.addr(transistor_4_out));  // open: we, oe, clk, din, dout
  Transistor #(.width(24)) transistor_4 (.in({24{1'b1}}), .out(transistor_4_out), .gate(subtractor_2_bout));
  ROM S_Table ();  // open: addr, data

  // Notes on the sheet:
  //   contents of S_Table (hex, n*v repeats v):
  //   29 2e 43 c9 a2 d8 7c 1 3d 36 54 a1 ec f0 6 13 20 4d 8a 2 6c 7d 38 3b 8a 1e 43 f4 c0 e0 b7 cd c5 7e
  //   7e 27 b6 5a 2f aa ab 9d dd e9 3 2c 5 aa 38 73 92 c6 c2 ca 81 4f dd 41 3 52 6e 81 d5 d 24 1b 3c 33 44
  //   a4 cf 9f 31 3c 50 50 28 cd 42 70 75 be 74 b1 42 84 b3 f5 71 17 3d 91 df f5 d4 41 cb fb 2f 7f b2 65
  //   14 a5 11 52 6d 51 82 c6 78 91 63 7f 3a bb 6d 29 c5 27 9 90 9f 31 7c b9 e 3e 53 de 86 77 d1 b1 87 81
  //   7c 41 59 fe ec e5 b0 82 38 2c 11 bc b8 92 b6 74 7b 22 b6 a6 9c b7 30 f3 9c 3f fb 5f c1 80 43 35 41
  //   15 f1 f6 d6 3b 7c 64 c8 c7 80 d2 fb fa b9 97 bf 4 94 e3 4c 13 c8 36 bc 8a e5 6e 6a e4 67 fa 5c eb 67
  //   74 a4 70 cf fd 87 8a 87 cd d 3 0 6d 26 48 88 8e 6d 9c 79 93 38 d6 96 30 4b 90 44 c9 fa 65 3b 42 90
  //   f8 b4 f5 1c 4c 46 20 f5 59 7c bb 45 5b 71 52 7a 6e 5b 8c
endmodule
