// Logisim project program_counter_poc.circ as structural Verilog: 1 circuit, main circuit main
module main (
);

  wire clock_1_out, clock_2_out, counter_2_carry, d_ff_1_q, not_1_out, not_2_out, not_3_out, not_4_out,
       not_5_out, pull_resistor_1_node, pull_resistor_3_node, pull_resistor_5_node, s_r_ff_1_q, xor_1_out;
  wire [7:0] counter_1_q, ram_1_dout;

  Clock clock_1 (.out(clock_1_out));
  S_R_Flip_Flop s_r_ff_1 (
    .S(pull_resistor_1_node), .R(s_r_ff_1_q), .clk(clock_1_out), .Q(s_r_ff_1_q));  // open: reset, Qn, preset
  Pull_Resistor pull_resistor_1 (.node(pull_resistor_1_node));
  Pull_Resistor #(.pull(1)) pull_resistor_2 (.node(s_r_ff_1_q));
  Pull_Resistor #(.pull(1)) pull_resistor_3 (.node(pull_resistor_3_node));
  Clock clock_2 (.out(clock_2_out));
  Counter counter_1 (
    .up(pull_resistor_3_node), .count(s_r_ff_1_q), .clk(clock_1_out), .Q(counter_1_q));  // open: clr, load, D, carry
  xor xor_1 (xor_1_out, clock_2_out, not_4_out);
  D_Flip_Flop d_ff_1 (.D(clock_2_out), .clk(xor_1_out), .Q(d_ff_1_q));  // open: Qn, preset, reset
  not not_1 (not_1_out, d_ff_1_q);
  Pull_Resistor pull_resistor_4 (.node(d_ff_1_q));
  not not_2 (not_2_out, not_1_out);
  RAM #(.readbehav("war")) ram_1 (
    .addr(counter_1_q), .oe(s_r_ff_1_q), .clk(clock_1_out), .dout(ram_1_dout));  // open: we, din
  not not_3 (not_3_out, not_2_out);
  not not_4 (not_4_out, not_3_out);
  Pull_Resistor #(.pull(1)) pull_resistor_5 (.node(pull_resistor_5_node));
  not not_5 (not_5_out, s_r_ff_1_q);
  Counter counter_2 (
    .load(s_r_ff_1_q), .up(pull_resistor_5_node), .count(not_5_out), .clk(clock_1_out), .D(ram_1_dout),
    .carry(counter_2_carry));  // open: clr, Q
endmodule
