// Logisim project riscv.circ as structural Verilog: 1 circuit, main circuit main
module main (
);

  wire and_5_out, button_1_out, comparator_1_eq, comparator_2_eq, comparator_3_eq, not_2_out, or_1_out,
       pull_resistor_1_node, pull_resistor_3_node, pull_resistor_6_node, pull_resistor_10_node,
       pull_resistor_13_node, pull_resistor_14_node, pull_resistor_17_node, pull_resistor_18_node,
       System_reset_q;
  wire [4:0] pull_resistor_16_node;
  wire [5:0] R_Type_Detector_out;
  wire [6:0] and_4_out;
  wire [7:0] and_2_out, bit_extender_1_out, Program_Data_data, pull_resistor_15_node;
  wire [11:0] pull_resistor_19_node;
  wire [24:5] controlled_buffer_12_out;
  wire [24:17] controlled_buffer_13_out;
  wire [31:0] adder_1_out, adder_2_out, and_1_out, and_6_out, bit_extender_2_out, bit_extender_3_out,
       controlled_buffer_4_out, controlled_buffer_8_out, controlled_buffer_10_out, Instruction_q,
       Program_Counter_q, register_1_q, register_2_q, register_3_q, register_4_q, register_5_q, register_6_q,
       register_7_q, register_8_q, register_9_q, register_10_q, register_11_q, register_12_q, register_13_q,
       register_14_q, register_15_q, register_16_q, register_17_q, register_18_q, register_19_q,
       register_20_q, register_21_q, register_22_q, register_23_q, register_24_q, register_25_q,
       register_26_q, register_27_q, register_28_q, register_29_q, register_30_q, register_31_q,
       shift_register_1_p6, transistor_1_out, transistor_6_out;
  wire [31:8] undriven;
  wire [31:12] controlled_buffer_16_out;
  wire [34:32] decoder_3_out0, decoder_3_out1, decoder_3_out2, decoder_3_out3, decoder_3_out4,
       decoder_3_out5, decoder_3_out6, decoder_3_out8, decoder_3_out9, decoder_3_out10, decoder_3_out11,
       decoder_3_out12, decoder_3_out13, decoder_3_out14, decoder_3_out15, decoder_3_out16, decoder_3_out17,
       decoder_3_out18, decoder_3_out19, decoder_3_out20, decoder_3_out21, decoder_3_out22, decoder_3_out23,
       decoder_3_out24, decoder_3_out25, decoder_3_out26, decoder_3_out27, decoder_3_out28, decoder_3_out29,
       decoder_3_out30, decoder_3_out31;
  wire [36:0] pull_resistor_8_node;

  Clock clock_1 (.out(pull_resistor_8_node[35]));
  Pull_Resistor pull_resistor_1 (.node(pull_resistor_1_node));
  Transistor #(.\type ("n"), .width(32)) transistor_1 (
    .in(register_1_q), .out(transistor_1_out), .gate(pull_resistor_8_node[32]));
  Register #(.width(32)) register_1 (
    .D(pull_resistor_8_node[31:0]), .en(pull_resistor_8_node[34]), .clk(pull_resistor_8_node[35]),
    .Q(register_1_q), .clr(pull_resistor_8_node[36]));
  Transistor #(.\type ("n"), .width(32)) transistor_2 (
    .in(register_2_q), .out(transistor_1_out), .gate(decoder_3_out15[32]));
  Register #(.width(32)) register_2 (
    .D(pull_resistor_8_node[31:0]), .en(decoder_3_out15[34]), .clk(pull_resistor_8_node[35]),
    .Q(register_2_q), .clr(pull_resistor_8_node[36]));
  Transistor #(.\type ("n"), .width(32)) transistor_3 (
    .in(register_3_q), .out(transistor_1_out), .gate(decoder_3_out23[32]));
  Register #(.width(32)) register_3 (
    .D(pull_resistor_8_node[31:0]), .en(decoder_3_out23[34]), .clk(pull_resistor_8_node[35]),
    .Q(register_3_q), .clr(pull_resistor_8_node[36]));
  Transistor #(.\type ("n"), .width(32)) transistor_4 (
    .in(register_4_q), .out(transistor_1_out), .gate(decoder_3_out31[32]));
  Register #(.width(32)) register_4 (
    .D(pull_resistor_8_node[31:0]), .en(decoder_3_out31[34]), .clk(pull_resistor_8_node[35]),
    .Q(register_4_q), .clr(pull_resistor_8_node[36]));
  Transistor #(.\type ("n"), .width(32)) transistor_5 (
    .in(register_5_q), .out(transistor_1_out), .gate(decoder_3_out6[32]));
  Transistor #(.\type ("n"), .width(32)) transistor_6 (
    .in(register_1_q), .out(transistor_6_out), .gate(pull_resistor_8_node[33]));
  Register #(.width(32)) register_5 (
    .D(pull_resistor_8_node[31:0]), .en(decoder_3_out6[34]), .clk(pull_resistor_8_node[35]),
    .Q(register_5_q), .clr(pull_resistor_8_node[36]));
  Transistor #(.\type ("n"), .width(32)) transistor_7 (
    .in(register_6_q), .out(transistor_1_out), .gate(decoder_3_out14[32]));
  Transistor #(.\type ("n"), .width(32)) transistor_8 (
    .in(register_2_q), .out(transistor_6_out), .gate(decoder_3_out15[33]));
  Register #(.width(32)) register_6 (
    .D(pull_resistor_8_node[31:0]), .en(decoder_3_out14[34]), .clk(pull_resistor_8_node[35]),
    .Q(register_6_q), .clr(pull_resistor_8_node[36]));
  Transistor #(.\type ("n"), .width(32)) transistor_9 (
    .in(register_7_q), .out(transistor_1_out), .gate(decoder_3_out22[32]));
  Transistor #(.\type ("n"), .width(32)) transistor_10 (
    .in(register_3_q), .out(transistor_6_out), .gate(decoder_3_out23[33]));
  Register #(.width(32)) register_7 (
    .D(pull_resistor_8_node[31:0]), .en(decoder_3_out22[34]), .clk(pull_resistor_8_node[35]),
    .Q(register_7_q), .clr(pull_resistor_8_node[36]));
  Transistor #(.\type ("n"), .width(32)) transistor_11 (
    .in(register_8_q), .out(transistor_1_out), .gate(decoder_3_out30[32]));
  Transistor #(.\type ("n"), .width(32)) transistor_12 (
    .in(register_4_q), .out(transistor_6_out), .gate(decoder_3_out31[33]));
  Register #(.width(32)) register_8 (
    .D(pull_resistor_8_node[31:0]), .en(decoder_3_out30[34]), .clk(pull_resistor_8_node[35]),
    .Q(register_8_q), .clr(pull_resistor_8_node[36]));
  S_R_Flip_Flop System_reset (
    .S(pull_resistor_1_node), .clk(pull_resistor_8_node[35]), .Q(System_reset_q), .reset(button_1_out),
    .preset(pull_resistor_8_node[35]));  // open: R, Qn
  Button button_1 (.out(button_1_out));
  Transistor #(.\type ("n"), .width(32)) transistor_13 (
    .in(register_9_q), .out(transistor_1_out), .gate(decoder_3_out5[32]));
  Transistor #(.\type ("n"), .width(32)) transistor_14 (
    .in(register_5_q), .out(transistor_6_out), .gate(decoder_3_out6[33]));
  Register #(.width(32)) register_9 (
    .D(pull_resistor_8_node[31:0]), .en(decoder_3_out5[34]), .clk(pull_resistor_8_node[35]),
    .Q(register_9_q), .clr(pull_resistor_8_node[36]));
  Transistor #(.\type ("n"), .width(32)) transistor_15 (
    .in(register_10_q), .out(transistor_1_out), .gate(decoder_3_out13[32]));
  Transistor #(.\type ("n"), .width(32)) transistor_16 (
    .in(register_6_q), .out(transistor_6_out), .gate(decoder_3_out14[33]));
  Register #(.width(32)) register_10 (
    .D(pull_resistor_8_node[31:0]), .en(decoder_3_out13[34]), .clk(pull_resistor_8_node[35]),
    .Q(register_10_q), .clr(pull_resistor_8_node[36]));
  Transistor #(.\type ("n"), .width(32)) transistor_17 (
    .in(register_11_q), .out(transistor_1_out), .gate(decoder_3_out21[32]));
  Transistor #(.\type ("n"), .width(32)) transistor_18 (
    .in(register_7_q), .out(transistor_6_out), .gate(decoder_3_out22[33]));
  Register #(.width(32)) register_11 (
    .D(pull_resistor_8_node[31:0]), .en(decoder_3_out21[34]), .clk(pull_resistor_8_node[35]),
    .Q(register_11_q), .clr(pull_resistor_8_node[36]));
  Transistor #(.\type ("n"), .width(32)) transistor_19 (
    .in(register_12_q), .out(transistor_1_out), .gate(decoder_3_out29[32]));
  Transistor #(.\type ("n"), .width(32)) transistor_20 (
    .in(register_8_q), .out(transistor_6_out), .gate(decoder_3_out30[33]));
  Register #(.width(32)) register_12 (
    .D(pull_resistor_8_node[31:0]), .en(decoder_3_out29[34]), .clk(pull_resistor_8_node[35]),
    .Q(register_12_q), .clr(pull_resistor_8_node[36]));
  Pull_Resistor pull_resistor_2 (.node(System_reset_q));
  Pull_Resistor #(.pull(1)) pull_resistor_3 (.node(pull_resistor_3_node));
  Transistor #(.\type ("n"), .width(32)) transistor_21 (
    .in(register_13_q), .out(transistor_1_out), .gate(decoder_3_out4[32]));
  Transistor #(.\type ("n"), .width(32)) transistor_22 (
    .in(register_9_q), .out(transistor_6_out), .gate(decoder_3_out5[33]));
  Register #(.width(32)) register_13 (
    .D(pull_resistor_8_node[31:0]), .en(decoder_3_out4[34]), .clk(pull_resistor_8_node[35]),
    .Q(register_13_q), .clr(pull_resistor_8_node[36]));
  Transistor #(.\type ("n"), .width(32)) transistor_23 (
    .in(register_14_q), .out(transistor_1_out), .gate(decoder_3_out12[32]));
  Transistor #(.\type ("n"), .width(32)) transistor_24 (
    .in(register_10_q), .out(transistor_6_out), .gate(decoder_3_out13[33]));
  Register #(.width(32)) register_14 (
    .D(pull_resistor_8_node[31:0]), .en(decoder_3_out12[34]), .clk(pull_resistor_8_node[35]),
    .Q(register_14_q), .clr(pull_resistor_8_node[36]));
  Transistor #(.\type ("n"), .width(32)) transistor_25 (
    .in(register_15_q), .out(transistor_1_out), .gate(decoder_3_out20[32]));
  Transistor #(.\type ("n"), .width(32)) transistor_26 (
    .in(register_11_q), .out(transistor_6_out), .gate(decoder_3_out21[33]));
  Register #(.width(32)) register_15 (
    .D(pull_resistor_8_node[31:0]), .en(decoder_3_out20[34]), .clk(pull_resistor_8_node[35]),
    .Q(register_15_q), .clr(pull_resistor_8_node[36]));
  Transistor #(.\type ("n"), .width(32)) transistor_27 (
    .in(register_16_q), .out(transistor_1_out), .gate(decoder_3_out28[32]));
  Transistor #(.\type ("n"), .width(32)) transistor_28 (
    .in(register_12_q), .out(transistor_6_out), .gate(decoder_3_out29[33]));
  Register #(.width(32)) register_16 (
    .D(pull_resistor_8_node[31:0]), .en(decoder_3_out28[34]), .clk(pull_resistor_8_node[35]),
    .Q(register_16_q), .clr(pull_resistor_8_node[36]));
  not not_1 (pull_resistor_8_node[36], System_reset_q);
  Pull_Resistor pull_resistor_4 (.node(R_Type_Detector_out[5]));
  Transistor #(.\type ("n"), .width(32)) transistor_29 (
    .in(register_17_q), .out(transistor_1_out), .gate(decoder_3_out3[32]));
  Transistor #(.\type ("n"), .width(32)) transistor_30 (
    .in(register_13_q), .out(transistor_6_out), .gate(decoder_3_out4[33]));
  Register #(.width(32)) register_17 (
    .D(pull_resistor_8_node[31:0]), .en(decoder_3_out3[34]), .clk(pull_resistor_8_node[35]),
    .Q(register_17_q), .clr(pull_resistor_8_node[36]));
  Transistor #(.\type ("n"), .width(32)) transistor_31 (
    .in(register_18_q), .out(transistor_1_out), .gate(decoder_3_out11[32]));
  Transistor #(.\type ("n"), .width(32)) transistor_32 (
    .in(register_14_q), .out(transistor_6_out), .gate(decoder_3_out12[33]));
  Register #(.width(32)) register_18 (
    .D(pull_resistor_8_node[31:0]), .en(decoder_3_out11[34]), .clk(pull_resistor_8_node[35]),
    .Q(register_18_q), .clr(pull_resistor_8_node[36]));
  Transistor #(.\type ("n"), .width(32)) transistor_33 (
    .in(register_19_q), .out(transistor_1_out), .gate(decoder_3_out19[32]));
  Transistor #(.\type ("n"), .width(32)) transistor_34 (
    .in(register_15_q), .out(transistor_6_out), .gate(decoder_3_out20[33]));
  Register #(.width(32)) register_19 (
    .D(pull_resistor_8_node[31:0]), .en(decoder_3_out19[34]), .clk(pull_resistor_8_node[35]),
    .Q(register_19_q), .clr(pull_resistor_8_node[36]));
  Transistor #(.\type ("n"), .width(32)) transistor_35 (
    .in(register_20_q), .out(transistor_1_out), .gate(decoder_3_out27[32]));
  Transistor #(.\type ("n"), .width(32)) transistor_36 (
    .in(register_16_q), .out(transistor_6_out), .gate(decoder_3_out28[33]));
  Register #(.width(32)) register_20 (
    .D(pull_resistor_8_node[31:0]), .en(decoder_3_out27[34]), .clk(pull_resistor_8_node[35]),
    .Q(register_20_q), .clr(pull_resistor_8_node[36]));
  Pull_Resistor pull_resistor_5 (.node(pull_resistor_8_node[36]));
  Counter #(.max('hffffffff), .ongoal("stay"), .width(32)) Program_Counter (
    .clr(pull_resistor_8_node[36]), .load(pull_resistor_6_node), .up(pull_resistor_3_node),
    .count(pull_resistor_3_node), .clk(pull_resistor_8_node[35]), .D(controlled_buffer_10_out),
    .Q(Program_Counter_q));  // open: carry
  Pull_Resistor pull_resistor_6 (.node(pull_resistor_6_node));
  assign pull_resistor_6_node = R_Type_Detector_out[5] ? 1'b1 : 1'bz;  // Controlled_Buffer controlled_buffer_1
  Transistor #(.\type ("n"), .width(32)) transistor_37 (
    .in(register_21_q), .out(transistor_1_out), .gate(decoder_3_out2[32]));
  Transistor #(.\type ("n"), .width(32)) transistor_38 (
    .in(register_17_q), .out(transistor_6_out), .gate(decoder_3_out3[33]));
  Register #(.width(32)) register_21 (
    .D(pull_resistor_8_node[31:0]), .en(decoder_3_out2[34]), .clk(pull_resistor_8_node[35]),
    .Q(register_21_q), .clr(pull_resistor_8_node[36]));
  Transistor #(.\type ("n"), .width(32)) transistor_39 (
    .in(register_22_q), .out(transistor_1_out), .gate(decoder_3_out10[32]));
  Transistor #(.\type ("n"), .width(32)) transistor_40 (
    .in(register_18_q), .out(transistor_6_out), .gate(decoder_3_out11[33]));
  Register #(.width(32)) register_22 (
    .D(pull_resistor_8_node[31:0]), .en(decoder_3_out10[34]), .clk(pull_resistor_8_node[35]),
    .Q(register_22_q), .clr(pull_resistor_8_node[36]));
  Transistor #(.\type ("n"), .width(32)) transistor_41 (
    .in(register_23_q), .out(transistor_1_out), .gate(decoder_3_out18[32]));
  Transistor #(.\type ("n"), .width(32)) transistor_42 (
    .in(register_19_q), .out(transistor_6_out), .gate(decoder_3_out19[33]));
  Register #(.width(32)) register_23 (
    .D(pull_resistor_8_node[31:0]), .en(decoder_3_out18[34]), .clk(pull_resistor_8_node[35]),
    .Q(register_23_q), .clr(pull_resistor_8_node[36]));
  Transistor #(.\type ("n"), .width(32)) transistor_43 (
    .in(register_24_q), .out(transistor_1_out), .gate(decoder_3_out26[32]));
  Transistor #(.\type ("n"), .width(32)) transistor_44 (
    .in(register_20_q), .out(transistor_6_out), .gate(decoder_3_out27[33]));
  Register #(.width(32)) register_24 (
    .D(pull_resistor_8_node[31:0]), .en(decoder_3_out26[34]), .clk(pull_resistor_8_node[35]),
    .Q(register_24_q), .clr(pull_resistor_8_node[36]));
  Transistor #(.\type ("n"), .width(32)) transistor_45 (
    .in(register_25_q), .out(transistor_1_out), .gate(decoder_3_out1[32]));
  Transistor #(.\type ("n"), .width(32)) transistor_46 (
    .in(register_21_q), .out(transistor_6_out), .gate(decoder_3_out2[33]));
  Register #(.width(32)) register_25 (
    .D(pull_resistor_8_node[31:0]), .en(decoder_3_out1[34]), .clk(pull_resistor_8_node[35]),
    .Q(register_25_q), .clr(pull_resistor_8_node[36]));
  Transistor #(.\type ("n"), .width(32)) transistor_47 (
    .in(register_26_q), .out(transistor_1_out), .gate(decoder_3_out9[32]));
  Transistor #(.\type ("n"), .width(32)) transistor_48 (
    .in(register_22_q), .out(transistor_6_out), .gate(decoder_3_out10[33]));
  Register #(.width(32)) register_26 (
    .D(pull_resistor_8_node[31:0]), .en(decoder_3_out9[34]), .clk(pull_resistor_8_node[35]),
    .Q(register_26_q), .clr(pull_resistor_8_node[36]));
  Transistor #(.\type ("n"), .width(32)) transistor_49 (
    .in(register_27_q), .out(transistor_1_out), .gate(decoder_3_out17[32]));
  Transistor #(.\type ("n"), .width(32)) transistor_50 (
    .in(register_23_q), .out(transistor_6_out), .gate(decoder_3_out18[33]));
  Register #(.width(32)) register_27 (
    .D(pull_resistor_8_node[31:0]), .en(decoder_3_out17[34]), .clk(pull_resistor_8_node[35]),
    .Q(register_27_q), .clr(pull_resistor_8_node[36]));
  Transistor #(.\type ("n"), .width(32)) transistor_51 (
    .in(register_28_q), .out(transistor_1_out), .gate(decoder_3_out25[32]));
  Transistor #(.\type ("n"), .width(32)) transistor_52 (
    .in(register_24_q), .out(transistor_6_out), .gate(decoder_3_out26[33]));
  Register #(.width(32)) register_28 (
    .D(pull_resistor_8_node[31:0]), .en(decoder_3_out25[34]), .clk(pull_resistor_8_node[35]),
    .Q(register_28_q), .clr(pull_resistor_8_node[36]));
  Transistor #(.\type ("n"), .width(32)) transistor_53 (
    .in(register_25_q), .out(transistor_6_out), .gate(decoder_3_out1[33]));
  assign transistor_1_out = decoder_3_out0[32] ? {32{1'b0}} : 32'bz;  // Controlled_Buffer controlled_buffer_2
  Transistor #(.\type ("n"), .width(32)) transistor_54 (
    .in(register_29_q), .out(transistor_1_out), .gate(decoder_3_out8[32]));
  Transistor #(.\type ("n"), .width(32)) transistor_55 (
    .in(register_26_q), .out(transistor_6_out), .gate(decoder_3_out9[33]));
  Register #(.width(32)) register_29 (
    .D(pull_resistor_8_node[31:0]), .en(decoder_3_out8[34]), .clk(pull_resistor_8_node[35]),
    .Q(register_29_q), .clr(pull_resistor_8_node[36]));
  Transistor #(.\type ("n"), .width(32)) transistor_56 (
    .in(register_30_q), .out(transistor_1_out), .gate(decoder_3_out16[32]));
  Transistor #(.\type ("n"), .width(32)) transistor_57 (
    .in(register_27_q), .out(transistor_6_out), .gate(decoder_3_out17[33]));
  Register #(.width(32)) register_30 (
    .D(pull_resistor_8_node[31:0]), .en(decoder_3_out16[34]), .clk(pull_resistor_8_node[35]),
    .Q(register_30_q), .clr(pull_resistor_8_node[36]));
  Transistor #(.\type ("n"), .width(32)) transistor_58 (
    .in(register_31_q), .out(transistor_1_out), .gate(decoder_3_out24[32]));
  Transistor #(.\type ("n"), .width(32)) transistor_59 (
    .in(register_28_q), .out(transistor_6_out), .gate(decoder_3_out25[33]));
  Register #(.width(32)) register_31 (
    .D(pull_resistor_8_node[31:0]), .en(decoder_3_out24[34]), .clk(pull_resistor_8_node[35]),
    .Q(register_31_q), .clr(pull_resistor_8_node[36]));
  // Probe on transistor_1_out
  // Probe on transistor_6_out
  assign transistor_6_out = decoder_3_out0[33] ? {32{1'b0}} : 32'bz;  // Controlled_Buffer controlled_buffer_3
  Transistor #(.\type ("n"), .width(32)) transistor_60 (
    .in(register_29_q), .out(transistor_6_out), .gate(decoder_3_out8[33]));
  Transistor #(.\type ("n"), .width(32)) transistor_61 (
    .in(register_30_q), .out(transistor_6_out), .gate(decoder_3_out16[33]));
  Transistor #(.\type ("n"), .width(32)) transistor_62 (
    .in(register_31_q), .out(transistor_6_out), .gate(decoder_3_out24[33]));
  assign and_1_out = Program_Counter_q & {undriven, 8'hfc};  // AND_Gate and_1, 32 bits wide
  // Probe on pull_resistor_8_node[31:0]
  Pull_Resistor #(.pull(1)) pull_resistor_7 (.node(transistor_6_out));
  Pull_Resistor #(.pull(1)) pull_resistor_8 (.node(pull_resistor_8_node[31:0]));
  Pull_Resistor #(.pull(1)) pull_resistor_9 (.node(transistor_1_out));
  Decoder #(.select(5)) decoder_1 (
    .out0(decoder_3_out0[32]), .out1(decoder_3_out1[32]), .out2(decoder_3_out2[32]),
    .out3(decoder_3_out3[32]), .out4(decoder_3_out4[32]), .out5(decoder_3_out5[32]),
    .out6(decoder_3_out6[32]), .out7(pull_resistor_8_node[32]), .out8(decoder_3_out8[32]),
    .out9(decoder_3_out9[32]), .out10(decoder_3_out10[32]), .out11(decoder_3_out11[32]),
    .out12(decoder_3_out12[32]), .out13(decoder_3_out13[32]), .out14(decoder_3_out14[32]),
    .out15(decoder_3_out15[32]), .out16(decoder_3_out16[32]), .out17(decoder_3_out17[32]),
    .out18(decoder_3_out18[32]), .out19(decoder_3_out19[32]), .out20(decoder_3_out20[32]),
    .out21(decoder_3_out21[32]), .out22(decoder_3_out22[32]), .out23(decoder_3_out23[32]),
    .out24(decoder_3_out24[32]), .out25(decoder_3_out25[32]), .out26(decoder_3_out26[32]),
    .out27(decoder_3_out27[32]), .out28(decoder_3_out28[32]), .out29(decoder_3_out29[32]),
    .out30(decoder_3_out30[32]), .out31(decoder_3_out31[32]), .sel(controlled_buffer_12_out[12:8]),
    .en(pull_resistor_10_node));
  Bit_Extender #(.in_width(32), .out_width(8), .\type ("zero")) bit_extender_1 (
    .in(Program_Counter_q), .out(bit_extender_1_out));
  Pull_Resistor #(.pull(1)) pull_resistor_10 (.node(pull_resistor_10_node));
  Decoder #(.select(5)) decoder_2 (
    .out0(decoder_3_out0[33]), .out1(decoder_3_out1[33]), .out2(decoder_3_out2[33]),
    .out3(decoder_3_out3[33]), .out4(decoder_3_out4[33]), .out5(decoder_3_out5[33]),
    .out6(decoder_3_out6[33]), .out7(pull_resistor_8_node[33]), .out8(decoder_3_out8[33]),
    .out9(decoder_3_out9[33]), .out10(decoder_3_out10[33]), .out11(decoder_3_out11[33]),
    .out12(decoder_3_out12[33]), .out13(decoder_3_out13[33]), .out14(decoder_3_out14[33]),
    .out15(decoder_3_out15[33]), .out16(decoder_3_out16[33]), .out17(decoder_3_out17[33]),
    .out18(decoder_3_out18[33]), .out19(decoder_3_out19[33]), .out20(decoder_3_out20[33]),
    .out21(decoder_3_out21[33]), .out22(decoder_3_out22[33]), .out23(decoder_3_out23[33]),
    .out24(decoder_3_out24[33]), .out25(decoder_3_out25[33]), .out26(decoder_3_out26[33]),
    .out27(decoder_3_out27[33]), .out28(decoder_3_out28[33]), .out29(decoder_3_out29[33]),
    .out30(decoder_3_out30[33]), .out31(decoder_3_out31[33]), .sel(controlled_buffer_12_out[17:13]),
    .en(pull_resistor_13_node));
  assign and_2_out = bit_extender_1_out & 8'h3;  // AND_Gate and_2, 8 bits wide
  Pull_Resistor pull_resistor_11 (.node(controlled_buffer_12_out[12:8]));
  Pull_Resistor pull_resistor_12 (.node(controlled_buffer_12_out[17:13]));
  Pull_Resistor #(.pull(1)) pull_resistor_13 (.node(pull_resistor_13_node));
  Pull_Resistor #(.pull(1)) pull_resistor_14 (.node(pull_resistor_14_node));
  Decoder #(.select(5)) decoder_3 (
    .out0(decoder_3_out0[34]), .out1(decoder_3_out1[34]), .out2(decoder_3_out2[34]),
    .out3(decoder_3_out3[34]), .out4(decoder_3_out4[34]), .out5(decoder_3_out5[34]),
    .out6(decoder_3_out6[34]), .out7(pull_resistor_8_node[34]), .out8(decoder_3_out8[34]),
    .out9(decoder_3_out9[34]), .out10(decoder_3_out10[34]), .out11(decoder_3_out11[34]),
    .out12(decoder_3_out12[34]), .out13(decoder_3_out13[34]), .out14(decoder_3_out14[34]),
    .out15(decoder_3_out15[34]), .out16(decoder_3_out16[34]), .out17(decoder_3_out17[34]),
    .out18(decoder_3_out18[34]), .out19(decoder_3_out19[34]), .out20(decoder_3_out20[34]),
    .out21(decoder_3_out21[34]), .out22(decoder_3_out22[34]), .out23(decoder_3_out23[34]),
    .out24(decoder_3_out24[34]), .out25(decoder_3_out25[34]), .out26(decoder_3_out26[34]),
    .out27(decoder_3_out27[34]), .out28(decoder_3_out28[34]), .out29(decoder_3_out29[34]),
    .out30(decoder_3_out30[34]), .out31(decoder_3_out31[34]), .sel(pull_resistor_16_node),
    .en(pull_resistor_14_node));
  Pull_Resistor pull_resistor_15 (.node(pull_resistor_15_node));
  ROM Program_Data (.addr(bit_extender_1_out), .data(Program_Data_data));
  Pull_Resistor pull_resistor_16 (.node(pull_resistor_16_node));
  Decoder #(.select(5)) decoder_4 (
    .out0(pull_resistor_8_node[36]), .out1(pull_resistor_8_node[36]), .out2(pull_resistor_8_node[36]),
    .out3(pull_resistor_8_node[36]), .out4(pull_resistor_8_node[36]), .out5(pull_resistor_8_node[36]),
    .out6(pull_resistor_8_node[36]), .out7(pull_resistor_8_node[36]), .out8(pull_resistor_8_node[36]),
    .out9(pull_resistor_8_node[36]), .out10(pull_resistor_8_node[36]), .out11(pull_resistor_8_node[36]),
    .out12(pull_resistor_8_node[36]), .out13(pull_resistor_8_node[36]), .out14(pull_resistor_8_node[36]),
    .out15(pull_resistor_8_node[36]), .out16(pull_resistor_8_node[36]), .out17(pull_resistor_8_node[36]),
    .out18(pull_resistor_8_node[36]), .out19(pull_resistor_8_node[36]), .out20(pull_resistor_8_node[36]),
    .out21(pull_resistor_8_node[36]), .out22(pull_resistor_8_node[36]), .out23(pull_resistor_8_node[36]),
    .out24(pull_resistor_8_node[36]), .out25(pull_resistor_8_node[36]), .out26(pull_resistor_8_node[36]),
    .out27(pull_resistor_8_node[36]), .out28(pull_resistor_8_node[36]), .out29(pull_resistor_8_node[36]),
    .out30(pull_resistor_8_node[36]), .out31(pull_resistor_8_node[36]));  // open: sel, en
  Comparator comparator_1 (.a(and_2_out), .b(pull_resistor_15_node), .eq(comparator_1_eq));  // open: gt, lt
  Pull_Resistor #(.pull(1)) pull_resistor_17 (.node(pull_resistor_17_node));
  Pull_Resistor pull_resistor_18 (.node(pull_resistor_18_node));
  // Shift_Register #(.length(4), .width(8)) shift_register_1: pin names not known; wires that end beside it: pull_resistor_8_node[36], pull_resistor_18_node, pull_resistor_17_node, pull_resistor_8_node[35], Program_Data_data, shift_register_1_p6[7:0], shift_register_1_p6[15:8], shift_register_1_p6[23:16], shift_register_1_p6[31:24]
  Register #(.width(32)) Instruction (
    .D(shift_register_1_p6), .en(comparator_1_eq), .clk(pull_resistor_8_node[35]), .Q(Instruction_q),
    .clr(pull_resistor_8_node[36]));
  Comparator #(.mode("unsigned"), .width(7)) comparator_2 (
    .a(Instruction_q[6:0]), .b(7'b1100111), .eq(comparator_2_eq));  // open: gt, lt
  assign bit_extender_2_out = {{12{controlled_buffer_16_out[31]}}, controlled_buffer_16_out};  // Bit_Extender bit_extender_2
  assign bit_extender_3_out = {{20{controlled_buffer_13_out[24]}}, {controlled_buffer_13_out[24], pull_resistor_16_node[0], controlled_buffer_13_out[22:17], pull_resistor_16_node[4:1]}};  // Bit_Extender bit_extender_3
  assign controlled_buffer_4_out = comparator_2_eq ? bit_extender_3_out : 32'bz;  // Controlled_Buffer controlled_buffer_4
  assign and_1_out = comparator_2_eq ? transistor_1_out : 32'bz;  // Controlled_Buffer controlled_buffer_5
  Pull_Resistor pull_resistor_19 (.node(pull_resistor_19_node));
  assign controlled_buffer_4_out = R_Type_Detector_out[5] ? bit_extender_2_out : 32'bz;  // Controlled_Buffer controlled_buffer_6
  // AND_Gate and_3 is placed but not wired
  assign and_4_out = Instruction_q[6:0] & 7'b0100000;  // AND_Gate and_4, 7 bits wide
  and and_5 (and_5_out, R_Type_Detector_out[5], not_2_out);
  assign controlled_buffer_4_out = and_5_out ? {controlled_buffer_16_out, pull_resistor_19_node} : 32'bz;  // Controlled_Buffer controlled_buffer_7
  Adder #(.width(32)) adder_1 (.a(and_1_out), .b(32'h4), .out(adder_1_out));  // open: cin, cout
  PLA #(.in_width(32), .out_width(1)) R_Type_Detector (.in(Instruction_q), .out(R_Type_Detector_out[0]));
  PLA #(.in_width(32), .out_width(1), .\table ("xxxxxxxxxxxxxxxxx000xxxxx1100111 1 # JALR\nxxxxxxxxxxxxxxxxxxx0xxxxx0000011 1 # LB LH LBU LHU\nxxxxxxxxxxxxxxxxx010xxxxx0000011 1 # LW\nxxxxxxxxxxxxxxxxx000xxxxx0010011 1 # ADDI\nxxxxxxxxxxxxxxxxx01xxxxxx0010011 1 # SLTI SLTIU\nxxxxxxxxxxxxxxxxx1x0xxxxx0010011 1 # XORI ORI\nxxxxxxxxxxxxxxxxx111xxxxx0010011 1 # ANDI\n0000000xxxxxxxxxxx01xxxxx0010011 1 # SLLI SRLI\n0100000xxxxxxxxxx101xxxxx0010011 1 # SRAI")) I_Type_Detector (
    .in(Instruction_q), .out(R_Type_Detector_out[1]));
  PLA #(.in_width(32), .out_width(1), .\table ("xxxxxxxxxxxxxxxxx0xxxxxxx1100011 1 # SB SH SW")) S_Type_Detector (
    .in(Instruction_q), .out(R_Type_Detector_out[2]));
  PLA #(.in_width(32), .out_width(1), .\table ("xxxxxxxxxxxxxxxxxx0xxxxxx1100011 1 # BEQ BNE BLT BGE\nxxxxxxxxxxxxxxxxx11xxxxxx1100011 1 # BLTU BGEU")) B_Type_Decoder (
    .in(Instruction_q), .out(R_Type_Detector_out[3]));
  PLA #(.in_width(32), .out_width(1), .\table ("00000000000000000000000000x10111 1 # LUI,AUIPC")) U_Type_Detector (
    .in(Instruction_q), .out(R_Type_Detector_out[4]));
  PLA #(.in_width(32), .out_width(1), .\table ("00000000000000000000000001101111 1 # JAL")) J_Type_Detector (
    .in(Instruction_q), .out(R_Type_Detector_out[5]));
  Comparator #(.mode("unsigned"), .width(7)) comparator_3 (
    .a(and_4_out), .b(7'b0100000), .eq(comparator_3_eq));  // open: gt, lt
  not not_2 (not_2_out, comparator_3_eq);
  assign controlled_buffer_8_out = comparator_3_eq ? {controlled_buffer_16_out, pull_resistor_19_node} : 32'bz;  // Controlled_Buffer controlled_buffer_8
  assign controlled_buffer_8_out = not_2_out ? adder_2_out : 32'bz;  // Controlled_Buffer controlled_buffer_9
  Adder #(.width(32)) adder_2 (.a(controlled_buffer_4_out), .b(and_1_out), .out(adder_2_out));  // open: cin, cout
  or or_1 (or_1_out, comparator_2_eq, R_Type_Detector_out[5]);
  assign controlled_buffer_10_out = R_Type_Detector_out[5] ? adder_2_out : 32'bz;  // Controlled_Buffer controlled_buffer_10
  assign pull_resistor_8_node[31:0] = or_1_out ? adder_1_out : 32'bz;  // Controlled_Buffer controlled_buffer_11
  assign {controlled_buffer_12_out, pull_resistor_16_node} = R_Type_Detector_out[0] ? Instruction_q[31:7] : 25'bz;  // Controlled_Buffer controlled_buffer_12
  assign {controlled_buffer_13_out[24], pull_resistor_16_node[0], controlled_buffer_13_out[22:17], pull_resistor_16_node[4:1], controlled_buffer_12_out[12:5], pull_resistor_16_node} = R_Type_Detector_out[1] ? Instruction_q[31:7] : 25'bz;  // Controlled_Buffer controlled_buffer_13
  assign {controlled_buffer_12_out, pull_resistor_16_node} = R_Type_Detector_out[2] ? Instruction_q[31:7] : 25'bz;  // Controlled_Buffer controlled_buffer_14
  assign {controlled_buffer_13_out[24], controlled_buffer_13_out[22:17], controlled_buffer_12_out[17:5], pull_resistor_16_node} = R_Type_Detector_out[3] ? Instruction_q[31:7] : 25'bz;  // Controlled_Buffer controlled_buffer_15
  assign {controlled_buffer_16_out, pull_resistor_16_node} = R_Type_Detector_out[4] ? Instruction_q[31:7] : 25'bz;  // Controlled_Buffer controlled_buffer_16
  assign {controlled_buffer_16_out[31], controlled_buffer_16_out[19:12], controlled_buffer_16_out[20], controlled_buffer_16_out[30:21], pull_resistor_16_node} = R_Type_Detector_out[5] ? Instruction_q[31:7] : 25'bz;  // Controlled_Buffer controlled_buffer_17
  assign pull_resistor_8_node[31:0] = R_Type_Detector_out[5] ? controlled_buffer_8_out : 32'bz;  // Controlled_Buffer controlled_buffer_18
  assign and_6_out = adder_2_out & 32'h2;  // AND_Gate and_6, 32 bits wide
  Controlled_Buffer #(.width(32)) controlled_buffer_19 (
    .out(controlled_buffer_10_out), .en(comparator_2_eq));  // open: in
  Subtractor subtractor_1 ();  // open: a, b, out, bin, bout
  Multiplier multiplier_1 ();  // open: a, b, out, cin, cout
  Divider divider_1 ();  // open: a, b, out, upper, rem
  Adder adder_3 ();  // open: a, b, out, cin, cout
  // Pins of 8 and 32 bits meet at {undriven, 8'hfc}

  // Notes on the sheet:
  //   32:rs1, 33:rs2, 34:rd, 35:clk, 36:rst
  //   x0
  //   system is fuckin weird
  //   PC Address
  //   rs1,rs2,rd
  //   rs1, rs2, rd
  //   programs load 8 bits at a time, but address space is 32 bits
  //   PC (read)
  //   PC (write)
  //   rs1 decoder
  //   rs2 decoder
  //   rd decoder
  //   contents of Program_Data (hex, n*v repeats v):
  //   8c 17 2a 37 2 74 f9 37 18 ba 58 37 10 2 48 37 72 e6 e2 37 5a 7e f4 37 58 73 e7 37 7c 2c c6 37 d6 8c
  //   73 37 b9 c9 c2 37 7e 22 94 37 43 42 d9 37 1c 6d bd 37 9c 68 5b 37 0 e 97 37 6e 76 97 37 9c 91 57 37
  //   30 50 d 37 bf 21 e8 37 4e c8 7 37 3 77 3f 37 e7 8a 94 37 3 9c 68 37 3d 26 3e 27 d2 83 1c 85 e4 2e 26
  //   5d da 52 b6 24 3f 9f 90 8f 88 8 e8 8a 6c 94 48 f5 8f 4a a0 db d6 c5 ca 68 5a 3d f1 95 bb 81 75 2e 24
  //   c1 4a 98 90 9a a3 74 90 db 76 5f f7 35 f7 4e 22 ce 6d 6d a 90 d8 83 d6 2f 6f f8 14 94 75 65 21 38 46
  //   85 8a 7c a2 62 30 dc 29 17 e6 e9 c c6 cc 37 2c e6 5e 8d 79 3a 4f a4 cf 63 bd e4 2 56 57 2b d3 75 a0
  //   97 51 68 71 de c 77 37 d8 72 2a a6 92 b6 74 17 50 c8 d0 2b 87 5a 85 3c 6d 63 2c 8d b9 34 12 4b 51 ef
  //   1f 9a 9 ae c4 38 33 42 d7 fc f1 54 d5 9 e5 a4 81
  //   rst decoder (unused)
  //   opcode
  //   full_instruction
  //   LUI
  //   AUIPC
  //   inst_type
  //   rd
  //   imm20
  //   opcode
  //   rd
  //   funct3
  //   rs1
  //   imm
  //   imm12
  //   OBJECTION! EXCEPTION! instruction-address-misaligned
  //   imm5
  //   funct7
  //   funct3
  //   rd
endmodule
