// Logisim project riscv_latest.circ as structural Verilog: 9 circuits, main circuit main
module main (
);

  wire and_1_out, button_1_out, clock_1_out, execution_block_1_addr_read, execution_block_1_addr_write,
       execution_block_1_incr_pc, execution_block_1_read_pc_next, execution_block_1_write_pc,
       mmu_block_1_busy, not_1_out, or_1_out, por_1_out, por_block_1_rst;
  wire [2:0] type_decoder_1_funct3;
  wire [4:0] type_decoder_1_rd_sel, type_decoder_1_rs1_sel, type_decoder_1_rs2_sel;
  wire [6:0] type_decoder_1_funct7, type_decoder_1_opcode;
  wire [19:0] type_decoder_1_imm;
  wire [31:0] controlled_buffer_1_out, controlled_buffer_2_out, execution_block_1_address_out,
       execution_block_1_data_bus_out, execution_block_1_rd, mmu_block_1_data_out, program_counter_1_instr,
       program_counter_1_pc_data_read, register_block_no_transistors_1_rs1,
       register_block_no_transistors_1_rs2;

  Button button_1 (.out(button_1_out));
  or or_1 (or_1_out, button_1_out, por_1_out);
  Clock clock_1 (.out(clock_1_out));
  POR por_1 (.out(por_1_out));
  and and_1 (and_1_out, clock_1_out, ~mmu_block_1_busy);  // AND_Gate
  por_block por_block_1 (.clk(clock_1_out), .rst_btn(or_1_out), .rst(por_block_1_rst));
  program_counter program_counter_1 (
    .instr(program_counter_1_instr), .pc_data_read(program_counter_1_pc_data_read), .clk(and_1_out),
    .rst(por_block_1_rst), .read_next(execution_block_1_read_pc_next),
    .write_enable(execution_block_1_write_pc), .pc_data_write(controlled_buffer_2_out),
    .incr_enable(execution_block_1_incr_pc));
  mmu_block mmu_block_1 (
    .data_in(execution_block_1_data_bus_out), .address_in(execution_block_1_address_out), .clk(clock_1_out),
    .write(execution_block_1_addr_write), .funct3(type_decoder_1_funct3), .read(execution_block_1_addr_read),
    .rst(por_block_1_rst), .data_out(mmu_block_1_data_out), .busy(mmu_block_1_busy));
  type_decoder type_decoder_1 (
    .instr(program_counter_1_instr), .opcode(type_decoder_1_opcode), .imm(type_decoder_1_imm),
    .funct7(type_decoder_1_funct7), .funct3(type_decoder_1_funct3), .rd_sel(type_decoder_1_rd_sel),
    .rs2_sel(type_decoder_1_rs2_sel), .rs1_sel(type_decoder_1_rs1_sel));  // open: invalid, instr_type
  register_block_no_transistors register_block_no_transistors_1 (
    .rs1(register_block_no_transistors_1_rs1), .rs2(register_block_no_transistors_1_rs2),
    .rd(controlled_buffer_1_out), .rs1_sel(type_decoder_1_rs1_sel), .rst(por_block_1_rst),
    .rs2_sel(type_decoder_1_rs2_sel), .rd_sel(type_decoder_1_rd_sel), .clk(and_1_out));
  not not_1 (not_1_out, execution_block_1_write_pc);
  execution_block execution_block_1 (
    .clk(and_1_out), .rst(por_block_1_rst), .imm(type_decoder_1_imm),
    .rs1(register_block_no_transistors_1_rs1), .pc_data(program_counter_1_pc_data_read),
    .funct7(type_decoder_1_funct7), .rs2(register_block_no_transistors_1_rs2),
    .data_bus_in(mmu_block_1_data_out), .funct3(type_decoder_1_funct3), .opcode(type_decoder_1_opcode),
    .rd(execution_block_1_rd), .read_pc_next(execution_block_1_read_pc_next),
    .addr_write(execution_block_1_addr_write), .addr_read(execution_block_1_addr_read),
    .data_bus_out(execution_block_1_data_bus_out), .address_out(execution_block_1_address_out),
    .write_pc(execution_block_1_write_pc), .incr_pc(execution_block_1_incr_pc));
  assign controlled_buffer_1_out = not_1_out ? execution_block_1_rd : 32'bz;  // Controlled_Buffer controlled_buffer_1
  assign controlled_buffer_2_out = execution_block_1_write_pc ? execution_block_1_rd : 32'bz;  // Controlled_Buffer controlled_buffer_2

  // Notes on the sheet:
  //   iowait
  //   4 cycle reset on poweron
endmodule

module register_block (
  input  [31:0] rd,
  input  [4:0] rs1_sel,
  input  clk,
  input  [4:0] rs2_sel,
  input  [4:0] rd_sel,
  input  rst,
  output [31:0] rs1,
  output [31:0] rs2
);

  wire pull_resistor_1_node, pull_resistor_2_node, pull_resistor_3_node;
  wire [31:0] x1_q, x2_q, x3_q, x4_q, x5_q, x6_q, x7_q, x8_q, x9_q, x10_q, x11_q, x12_q, x13_q, x14_q, x15_q,
       x16_q, x17_q, x18_q, x19_q, x20_q, x21_q, x22_q, x23_q, x24_q, x25_q, x26_q, x27_q, x28_q, x29_q,
       x30_q, x31_q;
  wire [34:32] decoder_3_out0, decoder_3_out1, decoder_3_out2, decoder_3_out3, decoder_3_out4,
       decoder_3_out5, decoder_3_out6, decoder_3_out7, decoder_3_out8, decoder_3_out9, decoder_3_out10,
       decoder_3_out11, decoder_3_out12, decoder_3_out13, decoder_3_out14, decoder_3_out15, decoder_3_out16,
       decoder_3_out17, decoder_3_out18, decoder_3_out19, decoder_3_out20, decoder_3_out21, decoder_3_out22,
       decoder_3_out23, decoder_3_out24, decoder_3_out25, decoder_3_out26, decoder_3_out27, decoder_3_out28,
       decoder_3_out29, decoder_3_out30, decoder_3_out31;

  Transistor #(.\type ("n"), .width(32)) transistor_1 (.in(x7_q), .out(rs1), .gate(decoder_3_out7[32]));
  Register #(.width(32)) x7 (.D(rd), .en(decoder_3_out7[34]), .clk(clk), .Q(x7_q), .clr(rst));
  Transistor #(.\type ("n"), .width(32)) transistor_2 (.in(x15_q), .out(rs1), .gate(decoder_3_out15[32]));
  Register #(.width(32)) x15 (.D(rd), .en(decoder_3_out15[34]), .clk(clk), .Q(x15_q), .clr(rst));
  Transistor #(.\type ("n"), .width(32)) transistor_3 (.in(x23_q), .out(rs1), .gate(decoder_3_out23[32]));
  Register #(.width(32)) x23 (.D(rd), .en(decoder_3_out23[34]), .clk(clk), .Q(x23_q), .clr(rst));
  Transistor #(.\type ("n"), .width(32)) transistor_4 (.in(x31_q), .out(rs1), .gate(decoder_3_out31[32]));
  Register #(.width(32)) x31 (.D(rd), .en(decoder_3_out31[34]), .clk(clk), .Q(x31_q), .clr(rst));
  Transistor #(.\type ("n"), .width(32)) transistor_5 (.in(x6_q), .out(rs1), .gate(decoder_3_out6[32]));
  Transistor #(.\type ("n"), .width(32)) transistor_6 (.in(x7_q), .out(rs2), .gate(decoder_3_out7[33]));
  Register #(.width(32)) x6 (.D(rd), .en(decoder_3_out6[34]), .clk(clk), .Q(x6_q), .clr(rst));
  Transistor #(.\type ("n"), .width(32)) transistor_7 (.in(x14_q), .out(rs1), .gate(decoder_3_out14[32]));
  Transistor #(.\type ("n"), .width(32)) transistor_8 (.in(x15_q), .out(rs2), .gate(decoder_3_out15[33]));
  Register #(.width(32)) x14 (.D(rd), .en(decoder_3_out14[34]), .clk(clk), .Q(x14_q), .clr(rst));
  Transistor #(.\type ("n"), .width(32)) transistor_9 (.in(x22_q), .out(rs1), .gate(decoder_3_out22[32]));
  Transistor #(.\type ("n"), .width(32)) transistor_10 (.in(x23_q), .out(rs2), .gate(decoder_3_out23[33]));
  Register #(.width(32)) x22 (.D(rd), .en(decoder_3_out22[34]), .clk(clk), .Q(x22_q), .clr(rst));
  Transistor #(.\type ("n"), .width(32)) transistor_11 (.in(x30_q), .out(rs1), .gate(decoder_3_out30[32]));
  Transistor #(.\type ("n"), .width(32)) transistor_12 (.in(x31_q), .out(rs2), .gate(decoder_3_out31[33]));
  Register #(.width(32)) x30 (.D(rd), .en(decoder_3_out30[34]), .clk(clk), .Q(x30_q), .clr(rst));
  Transistor #(.\type ("n"), .width(32)) transistor_13 (.in(x5_q), .out(rs1), .gate(decoder_3_out5[32]));
  Transistor #(.\type ("n"), .width(32)) transistor_14 (.in(x6_q), .out(rs2), .gate(decoder_3_out6[33]));
  Register #(.width(32)) x5 (.D(rd), .en(decoder_3_out5[34]), .clk(clk), .Q(x5_q), .clr(rst));
  Transistor #(.\type ("n"), .width(32)) transistor_15 (.in(x13_q), .out(rs1), .gate(decoder_3_out13[32]));
  Transistor #(.\type ("n"), .width(32)) transistor_16 (.in(x14_q), .out(rs2), .gate(decoder_3_out14[33]));
  Register #(.width(32)) x13 (.D(rd), .en(decoder_3_out13[34]), .clk(clk), .Q(x13_q), .clr(rst));
  Transistor #(.\type ("n"), .width(32)) transistor_17 (.in(x21_q), .out(rs1), .gate(decoder_3_out21[32]));
  Transistor #(.\type ("n"), .width(32)) transistor_18 (.in(x22_q), .out(rs2), .gate(decoder_3_out22[33]));
  Register #(.width(32)) x21 (.D(rd), .en(decoder_3_out21[34]), .clk(clk), .Q(x21_q), .clr(rst));
  Transistor #(.\type ("n"), .width(32)) transistor_19 (.in(x29_q), .out(rs1), .gate(decoder_3_out29[32]));
  Transistor #(.\type ("n"), .width(32)) transistor_20 (.in(x30_q), .out(rs2), .gate(decoder_3_out30[33]));
  Register #(.width(32)) x29 (.D(rd), .en(decoder_3_out29[34]), .clk(clk), .Q(x29_q), .clr(rst));
  Transistor #(.\type ("n"), .width(32)) transistor_21 (.in(x4_q), .out(rs1), .gate(decoder_3_out4[32]));
  Transistor #(.\type ("n"), .width(32)) transistor_22 (.in(x5_q), .out(rs2), .gate(decoder_3_out5[33]));
  Register #(.width(32)) x4 (.D(rd), .en(decoder_3_out4[34]), .clk(clk), .Q(x4_q), .clr(rst));
  Transistor #(.\type ("n"), .width(32)) transistor_23 (.in(x12_q), .out(rs1), .gate(decoder_3_out12[32]));
  Transistor #(.\type ("n"), .width(32)) transistor_24 (.in(x13_q), .out(rs2), .gate(decoder_3_out13[33]));
  Register #(.width(32)) x12 (.D(rd), .en(decoder_3_out12[34]), .clk(clk), .Q(x12_q), .clr(rst));
  Transistor #(.\type ("n"), .width(32)) transistor_25 (.in(x20_q), .out(rs1), .gate(decoder_3_out20[32]));
  Transistor #(.\type ("n"), .width(32)) transistor_26 (.in(x21_q), .out(rs2), .gate(decoder_3_out21[33]));
  Register #(.width(32)) x20 (.D(rd), .en(decoder_3_out20[34]), .clk(clk), .Q(x20_q), .clr(rst));
  Transistor #(.\type ("n"), .width(32)) transistor_27 (.in(x28_q), .out(rs1), .gate(decoder_3_out28[32]));
  Transistor #(.\type ("n"), .width(32)) transistor_28 (.in(x29_q), .out(rs2), .gate(decoder_3_out29[33]));
  Register #(.width(32)) x28 (.D(rd), .en(decoder_3_out28[34]), .clk(clk), .Q(x28_q), .clr(rst));
  Transistor #(.\type ("n"), .width(32)) transistor_29 (.in(x3_q), .out(rs1), .gate(decoder_3_out3[32]));
  Transistor #(.\type ("n"), .width(32)) transistor_30 (.in(x4_q), .out(rs2), .gate(decoder_3_out4[33]));
  Register #(.width(32)) x3 (.D(rd), .en(decoder_3_out3[34]), .clk(clk), .Q(x3_q), .clr(rst));
  Transistor #(.\type ("n"), .width(32)) transistor_31 (.in(x11_q), .out(rs1), .gate(decoder_3_out11[32]));
  Transistor #(.\type ("n"), .width(32)) transistor_32 (.in(x12_q), .out(rs2), .gate(decoder_3_out12[33]));
  Register #(.width(32)) x11 (.D(rd), .en(decoder_3_out11[34]), .clk(clk), .Q(x11_q), .clr(rst));
  Transistor #(.\type ("n"), .width(32)) transistor_33 (.in(x19_q), .out(rs1), .gate(decoder_3_out19[32]));
  Transistor #(.\type ("n"), .width(32)) transistor_34 (.in(x20_q), .out(rs2), .gate(decoder_3_out20[33]));
  Register #(.width(32)) x19 (.D(rd), .en(decoder_3_out19[34]), .clk(clk), .Q(x19_q), .clr(rst));
  Transistor #(.\type ("n"), .width(32)) transistor_35 (.in(x27_q), .out(rs1), .gate(decoder_3_out27[32]));
  Transistor #(.\type ("n"), .width(32)) transistor_36 (.in(x28_q), .out(rs2), .gate(decoder_3_out28[33]));
  Register #(.width(32)) x27 (.D(rd), .en(decoder_3_out27[34]), .clk(clk), .Q(x27_q), .clr(rst));
  Transistor #(.\type ("n"), .width(32)) transistor_37 (.in(x2_q), .out(rs1), .gate(decoder_3_out2[32]));
  Transistor #(.\type ("n"), .width(32)) transistor_38 (.in(x3_q), .out(rs2), .gate(decoder_3_out3[33]));
  Register #(.width(32)) x2 (.D(rd), .en(decoder_3_out2[34]), .clk(clk), .Q(x2_q), .clr(rst));
  Transistor #(.\type ("n"), .width(32)) transistor_39 (.in(x10_q), .out(rs1), .gate(decoder_3_out10[32]));
  Transistor #(.\type ("n"), .width(32)) transistor_40 (.in(x11_q), .out(rs2), .gate(decoder_3_out11[33]));
  Register #(.width(32)) x10 (.D(rd), .en(decoder_3_out10[34]), .clk(clk), .Q(x10_q), .clr(rst));
  Transistor #(.\type ("n"), .width(32)) transistor_41 (.in(x18_q), .out(rs1), .gate(decoder_3_out18[32]));
  Transistor #(.\type ("n"), .width(32)) transistor_42 (.in(x19_q), .out(rs2), .gate(decoder_3_out19[33]));
  Register #(.width(32)) x18 (.D(rd), .en(decoder_3_out18[34]), .clk(clk), .Q(x18_q), .clr(rst));
  Transistor #(.\type ("n"), .width(32)) transistor_43 (.in(x26_q), .out(rs1), .gate(decoder_3_out26[32]));
  Transistor #(.\type ("n"), .width(32)) transistor_44 (.in(x27_q), .out(rs2), .gate(decoder_3_out27[33]));
  Register #(.width(32)) x26 (.D(rd), .en(decoder_3_out26[34]), .clk(clk), .Q(x26_q), .clr(rst));
  Transistor #(.\type ("n"), .width(32)) transistor_45 (.in(x1_q), .out(rs1), .gate(decoder_3_out1[32]));
  Transistor #(.\type ("n"), .width(32)) transistor_46 (.in(x2_q), .out(rs2), .gate(decoder_3_out2[33]));
  Register #(.width(32)) x1 (.D(rd), .en(decoder_3_out1[34]), .clk(clk), .Q(x1_q), .clr(rst));
  Transistor #(.\type ("n"), .width(32)) transistor_47 (.in(x9_q), .out(rs1), .gate(decoder_3_out9[32]));
  Transistor #(.\type ("n"), .width(32)) transistor_48 (.in(x10_q), .out(rs2), .gate(decoder_3_out10[33]));
  Register #(.width(32)) x9 (.D(rd), .en(decoder_3_out9[34]), .clk(clk), .Q(x9_q), .clr(rst));
  Transistor #(.\type ("n"), .width(32)) transistor_49 (.in(x17_q), .out(rs1), .gate(decoder_3_out17[32]));
  Transistor #(.\type ("n"), .width(32)) transistor_50 (.in(x18_q), .out(rs2), .gate(decoder_3_out18[33]));
  Register #(.width(32)) x17 (.D(rd), .en(decoder_3_out17[34]), .clk(clk), .Q(x17_q), .clr(rst));
  Transistor #(.\type ("n"), .width(32)) transistor_51 (.in(x25_q), .out(rs1), .gate(decoder_3_out25[32]));
  Transistor #(.\type ("n"), .width(32)) transistor_52 (.in(x26_q), .out(rs2), .gate(decoder_3_out26[33]));
  Register #(.width(32)) x25 (.D(rd), .en(decoder_3_out25[34]), .clk(clk), .Q(x25_q), .clr(rst));
  Transistor #(.\type ("n"), .width(32)) transistor_53 (.in(x1_q), .out(rs2), .gate(decoder_3_out1[33]));
  assign rs1 = decoder_3_out0[32] ? {32{1'b0}} : 32'bz;  // Controlled_Buffer controlled_buffer_1
  Transistor #(.\type ("n"), .width(32)) transistor_54 (.in(x8_q), .out(rs1), .gate(decoder_3_out8[32]));
  Transistor #(.\type ("n"), .width(32)) transistor_55 (.in(x9_q), .out(rs2), .gate(decoder_3_out9[33]));
  Register #(.width(32)) x8 (.D(rd), .en(decoder_3_out8[34]), .clk(clk), .Q(x8_q), .clr(rst));
  Transistor #(.\type ("n"), .width(32)) transistor_56 (.in(x16_q), .out(rs1), .gate(decoder_3_out16[32]));
  Transistor #(.\type ("n"), .width(32)) transistor_57 (.in(x17_q), .out(rs2), .gate(decoder_3_out17[33]));
  Register #(.width(32)) x16 (.D(rd), .en(decoder_3_out16[34]), .clk(clk), .Q(x16_q), .clr(rst));
  Transistor #(.\type ("n"), .width(32)) transistor_58 (.in(x24_q), .out(rs1), .gate(decoder_3_out24[32]));
  Transistor #(.\type ("n"), .width(32)) transistor_59 (.in(x25_q), .out(rs2), .gate(decoder_3_out25[33]));
  Register #(.width(32)) x24 (.D(rd), .en(decoder_3_out24[34]), .clk(clk), .Q(x24_q), .clr(rst));
  assign rs2 = decoder_3_out0[33] ? {32{1'b0}} : 32'bz;  // Controlled_Buffer controlled_buffer_2
  Transistor #(.\type ("n"), .width(32)) transistor_60 (.in(x8_q), .out(rs2), .gate(decoder_3_out8[33]));
  Transistor #(.\type ("n"), .width(32)) transistor_61 (.in(x16_q), .out(rs2), .gate(decoder_3_out16[33]));
  Transistor #(.\type ("n"), .width(32)) transistor_62 (.in(x24_q), .out(rs2), .gate(decoder_3_out24[33]));
  Decoder #(.select(5)) decoder_1 (
    .out0(decoder_3_out0[32]), .out1(decoder_3_out1[32]), .out2(decoder_3_out2[32]),
    .out3(decoder_3_out3[32]), .out4(decoder_3_out4[32]), .out5(decoder_3_out5[32]),
    .out6(decoder_3_out6[32]), .out7(decoder_3_out7[32]), .out8(decoder_3_out8[32]),
    .out9(decoder_3_out9[32]), .out10(decoder_3_out10[32]), .out11(decoder_3_out11[32]),
    .out12(decoder_3_out12[32]), .out13(decoder_3_out13[32]), .out14(decoder_3_out14[32]),
    .out15(decoder_3_out15[32]), .out16(decoder_3_out16[32]), .out17(decoder_3_out17[32]),
    .out18(decoder_3_out18[32]), .out19(decoder_3_out19[32]), .out20(decoder_3_out20[32]),
    .out21(decoder_3_out21[32]), .out22(decoder_3_out22[32]), .out23(decoder_3_out23[32]),
    .out24(decoder_3_out24[32]), .out25(decoder_3_out25[32]), .out26(decoder_3_out26[32]),
    .out27(decoder_3_out27[32]), .out28(decoder_3_out28[32]), .out29(decoder_3_out29[32]),
    .out30(decoder_3_out30[32]), .out31(decoder_3_out31[32]), .sel(rs1_sel), .en(pull_resistor_1_node));
  Pull_Resistor #(.pull(1)) pull_resistor_1 (.node(pull_resistor_1_node));
  Decoder #(.select(5)) decoder_2 (
    .out0(decoder_3_out0[33]), .out1(decoder_3_out1[33]), .out2(decoder_3_out2[33]),
    .out3(decoder_3_out3[33]), .out4(decoder_3_out4[33]), .out5(decoder_3_out5[33]),
    .out6(decoder_3_out6[33]), .out7(decoder_3_out7[33]), .out8(decoder_3_out8[33]),
    .out9(decoder_3_out9[33]), .out10(decoder_3_out10[33]), .out11(decoder_3_out11[33]),
    .out12(decoder_3_out12[33]), .out13(decoder_3_out13[33]), .out14(decoder_3_out14[33]),
    .out15(decoder_3_out15[33]), .out16(decoder_3_out16[33]), .out17(decoder_3_out17[33]),
    .out18(decoder_3_out18[33]), .out19(decoder_3_out19[33]), .out20(decoder_3_out20[33]),
    .out21(decoder_3_out21[33]), .out22(decoder_3_out22[33]), .out23(decoder_3_out23[33]),
    .out24(decoder_3_out24[33]), .out25(decoder_3_out25[33]), .out26(decoder_3_out26[33]),
    .out27(decoder_3_out27[33]), .out28(decoder_3_out28[33]), .out29(decoder_3_out29[33]),
    .out30(decoder_3_out30[33]), .out31(decoder_3_out31[33]), .sel(rs2_sel), .en(pull_resistor_2_node));
  Pull_Resistor #(.pull(1)) pull_resistor_2 (.node(pull_resistor_2_node));
  Pull_Resistor #(.pull(1)) pull_resistor_3 (.node(pull_resistor_3_node));
  Decoder #(.select(5)) decoder_3 (
    .out0(decoder_3_out0[34]), .out1(decoder_3_out1[34]), .out2(decoder_3_out2[34]),
    .out3(decoder_3_out3[34]), .out4(decoder_3_out4[34]), .out5(decoder_3_out5[34]),
    .out6(decoder_3_out6[34]), .out7(decoder_3_out7[34]), .out8(decoder_3_out8[34]),
    .out9(decoder_3_out9[34]), .out10(decoder_3_out10[34]), .out11(decoder_3_out11[34]),
    .out12(decoder_3_out12[34]), .out13(decoder_3_out13[34]), .out14(decoder_3_out14[34]),
    .out15(decoder_3_out15[34]), .out16(decoder_3_out16[34]), .out17(decoder_3_out17[34]),
    .out18(decoder_3_out18[34]), .out19(decoder_3_out19[34]), .out20(decoder_3_out20[34]),
    .out21(decoder_3_out21[34]), .out22(decoder_3_out22[34]), .out23(decoder_3_out23[34]),
    .out24(decoder_3_out24[34]), .out25(decoder_3_out25[34]), .out26(decoder_3_out26[34]),
    .out27(decoder_3_out27[34]), .out28(decoder_3_out28[34]), .out29(decoder_3_out29[34]),
    .out30(decoder_3_out30[34]), .out31(decoder_3_out31[34]), .sel(rd_sel), .en(pull_resistor_3_node));
  Decoder #(.select(5)) decoder_4 (
    .out0(rst), .out1(rst), .out2(rst), .out3(rst), .out4(rst), .out5(rst), .out6(rst), .out7(rst),
    .out8(rst), .out9(rst), .out10(rst), .out11(rst), .out12(rst), .out13(rst), .out14(rst), .out15(rst),
    .out16(rst), .out17(rst), .out18(rst), .out19(rst), .out20(rst), .out21(rst), .out22(rst), .out23(rst),
    .out24(rst), .out25(rst), .out26(rst), .out27(rst), .out28(rst), .out29(rst), .out30(rst), .out31(rst));  // open: sel, en

  // Notes on the sheet:
  //   rs1: pull=down
  //   rs2: pull=down
  //   rd: pull=up
  //   rs1_sel: pull=down
  //   rst: pull=down
  //   rs2_sel: pull=down
  //   rd_sel: pull=down
  //   x0
  //   rs1 decoder
  //   rs2 decoder
  //   rd decoder
endmodule

module type_decoder (
  input  [31:0] instr,
  output invalid,
  output [5:0] instr_type,
  output [6:0] opcode,
  output [19:0] imm,
  output [6:0] funct7,
  output [2:0] funct3,
  output [4:0] rd_sel,
  output [4:0] rs2_sel,
  output [4:0] rs1_sel
);

  wire [2:0] Data_decoder_out;

  PLA #(.in_width(32), .out_width(3), .\table ("0x00000xxxxxxxxxx000xxxxx0110011 001 # ADD SUB\n0000000xxxxxxxxxx001xxxxx0110011 001 # SLL\n0000000xxxxxxxxxx01xxxxxx0110011 001 # SLT SLTU\n0000000xxxxxxxxxx100xxxxx0110011 001 # XOR\n0x00000xxxxxxxxxx101xxxxx0110011 001 # SRL SRA\n0000000xxxxxxxxxx11xxxxxx0110011 001 # OR AND\nxxxxxxxxxxxxxxxxx000xxxxx1100111 010 # JALR\nxxxxxxxxxxxxxxxxxxx0xxxxx0000011 010 # LB LH LBU LHU\nxxxxxxxxxxxxxxxxx010xxxxx0000011 010 # LW\nxxxxxxxxxxxxxxxxx000xxxxx0010011 010 # ADDI\nxxxxxxxxxxxxxxxxx01xxxxxx0010011 010 # SLTI SLTIU\nxxxxxxxxxxxxxxxxx1x0xxxxx0010011 010 # XORI ORI\nxxxxxxxxxxxxxxxxx111xxxxx0010011 010 # ANDI\n0000000xxxxxxxxxxx01xxxxx0010011 010 # SLLI SRLI\n0100000xxxxxxxxxx101xxxxx0010011 010 # SRAI\nxxxxxxxxxxxxxxxxx0xxxxxxx1100011 011 # SB SH SW\nxxxxxxxxxxxxxxxxxx0xxxxxx1100011 100 # BEQ BNE BLT BGE\nxxxxxxxxxxxxxxxxx11xxxxxx1100011 100 # BLTU BGEU\nxxxxxxxxxxxxxxxxxxxxxxxxx0x10111 101 # LUI AUIPC\nxxxxxxxxxxxxxxxxxxxxxxxxx1101111 110 # JAL")) Data_decoder (
    .in(instr), .out(Data_decoder_out));
  Decoder #(.select(3)) decoder_1 (
    .out0(invalid), .out1(instr_type[0]), .out2(instr_type[1]), .out3(instr_type[2]), .out4(instr_type[3]),
    .out5(instr_type[4]), .out6(instr_type[5]), .sel(Data_decoder_out), .en(1'b1));  // open: out7
  assign {funct7, rs2_sel, rs1_sel, funct3, rd_sel} = instr_type[0] ? instr[31:7] : 25'bz;  // Controlled_Buffer controlled_buffer_1
  assign {imm[11:0], rs1_sel, funct3, rd_sel} = instr_type[1] ? instr[31:7] : 25'bz;  // Controlled_Buffer controlled_buffer_2
  assign {imm[11:5], rs2_sel, rs1_sel, funct3, imm[4:0]} = instr_type[2] ? instr[31:7] : 25'bz;  // Controlled_Buffer controlled_buffer_3
  assign {imm[11], imm[9:4], rs2_sel, rs1_sel, funct3, imm[3:0], imm[10]} = instr_type[3] ? instr[31:7] : 25'bz;  // Controlled_Buffer controlled_buffer_4
  assign {imm, rd_sel} = instr_type[4] ? instr[31:7] : 25'bz;  // Controlled_Buffer controlled_buffer_5
  assign {imm[19], imm[7:0], imm[8], imm[18:9], rd_sel} = instr_type[5] ? instr[31:7] : 25'bz;  // Controlled_Buffer controlled_buffer_6

  assign opcode = instr[6:0];

  // Notes on the sheet:
  //   rd_sel: pull=down
  //   rs2_sel: pull=down
  //   rs1_sel: pull=down
  //   opcode: pull=down
  //   imm: pull=down
  //   funct7: pull=down
  //   funct3: pull=down
  //   U/J imm20
  //   I/B/S imm12
  //   funct7
  //   funct3
endmodule

module doc (
);

  wire controlled_buffer_1_out, controlled_buffer_2_out, controlled_buffer_6_out, controlled_buffer_8_out,
       controlled_buffer_9_out, undriven, undriven_2, undriven_3, undriven_4, undriven_5, undriven_6,
       undriven_7, undriven_8, undriven_9, undriven_10;

  assign controlled_buffer_1_out = undriven_10 ? undriven_7 : 1'bz;  // Controlled_Buffer controlled_buffer_1
  assign controlled_buffer_2_out = undriven_10 ? undriven_4 : 1'bz;  // Controlled_Buffer controlled_buffer_2
  assign controlled_buffer_2_out = undriven_10 ? undriven : 1'bz;  // Controlled_Buffer controlled_buffer_3
  assign controlled_buffer_2_out = undriven_10 ? undriven_2 : 1'bz;  // Controlled_Buffer controlled_buffer_4
  assign controlled_buffer_1_out = undriven_10 ? undriven_3 : 1'bz;  // Controlled_Buffer controlled_buffer_5
  assign controlled_buffer_6_out = undriven_10 ? undriven_8 : 1'bz;  // Controlled_Buffer controlled_buffer_6
  assign controlled_buffer_6_out = undriven_10 ? undriven_9 : 1'bz;  // Controlled_Buffer controlled_buffer_7
  assign controlled_buffer_8_out = undriven_10 ? undriven_5 : 1'bz;  // Controlled_Buffer controlled_buffer_8
  assign controlled_buffer_9_out = undriven_10 ? undriven_6 : 1'bz;  // Controlled_Buffer controlled_buffer_9

  // Notes on the sheet:
  //   R
  //   S
  //   I
  //   Instruction Decode Logic
  //   B
  //   Clock divider (/2)
  //   U
  //   J
  //   stall/resume
  //   Opcode
  //   Valid?
  //   Control Logic
  //   Inputs (from elsewhere on the board)
  //   Instruction
  //   pc
  //   rs1
  //   rs2
  //   rd
  //   Input J/U imm 20
  //   Input S/B/I imm12
  //   function7
  //   function3
  //   Input A-2; Input B-2
  //   Output-1; Output-2
  //   Transform A; Transform B (or zero)
  //   +4
  //   Data I/O Selector
  //   imm12 activated?
  //   Input A-1
  //   Input B-1
  //   Output-1
  //   <- connect as appropriate; switch using clock divider
  //   Input A-2
  //   Input B-2
  //   Output-2
  //   Clock cycle 1: reset
  //   Instruction cycle is 4 clock cycles; load and execute are parallel
  //   Any branch instruction incurs a 6 cycle penalty (4 to load, 2 to decode)
  //   Instructions may perform up to 2 data transforms per instruction cycle
  //   TODO: Instructions longer than 4 cycles? Stall the shift register load to inst?
  //   System is limited by ROM access; faster instruction load? pipeline?
  //   Clock cycle 4n+2: load instruction into shift register
  //   Clock cycle 4n+6: load shift register into decode register
  //   Data transform block
endmodule

module program_counter (
  input  clk,
  input  rst,
  input  incr_enable,
  input  read_next,
  input  write_enable,
  input  [31:0] pc_data_write,
  output [31:0] instr,
  output [31:0] pc_data_read
);

  wire and_1_out, and_2_out, and_3_out, and_4_out, and_5_out, comparator_1_eq, comparator_2_lt,
       counter_1_carry, not_1_out, not_2_out, not_3_out, not_4_out, or_1_out, or_2_out;
  wire [1:0] counter_1_q;
  wire [7:0] bit_extender_1_out, Init_firmware_data;
  wire [31:0] adder_1_out, controlled_buffer_1_out, controlled_buffer_2_out, controlled_buffer_6_out,
       controlled_buffer_9_out, PC_q, shift_register_1_p6;

  or or_1 (or_1_out, and_5_out, rst, write_enable);
  assign controlled_buffer_1_out = write_enable ? pc_data_write : 32'bz;  // Controlled_Buffer controlled_buffer_1
  assign controlled_buffer_2_out = rst ? {32{1'b0}} : 32'bz;  // Controlled_Buffer controlled_buffer_2
  Register #(.width(32)) PC (.D(controlled_buffer_2_out), .en(or_1_out), .clk(clk), .Q(PC_q));  // open: clr
  assign controlled_buffer_2_out = and_1_out ? controlled_buffer_1_out : 32'bz;  // Controlled_Buffer controlled_buffer_3
  and and_1 (and_1_out, ~incr_enable, write_enable);  // AND_Gate
  not not_1 (not_1_out, read_next);
  not not_2 (not_2_out, write_enable);
  and and_2 (and_2_out, incr_enable, write_enable);
  and and_3 (and_3_out, read_next, not_2_out);
  and and_4 (and_4_out, not_1_out, not_2_out);
  assign pc_data_read = and_4_out ? PC_q : 32'bz;  // Controlled_Buffer controlled_buffer_4
  assign pc_data_read = and_3_out ? controlled_buffer_9_out : 32'bz;  // Controlled_Buffer controlled_buffer_5
  assign controlled_buffer_6_out = not_3_out ? 32'h4 : 32'bz;  // Controlled_Buffer controlled_buffer_6
  not not_3 (not_3_out, and_2_out);
  assign controlled_buffer_6_out = and_2_out ? controlled_buffer_1_out : 32'bz;  // Controlled_Buffer controlled_buffer_7
  assign controlled_buffer_2_out = and_2_out ? adder_1_out : 32'bz;  // Controlled_Buffer controlled_buffer_8
  or or_2 (or_2_out, rst, write_enable);
  assign controlled_buffer_9_out = comparator_2_lt ? adder_1_out : 32'bz;  // Controlled_Buffer controlled_buffer_9
  Adder #(.width(32)) adder_1 (.a(controlled_buffer_6_out), .b(PC_q), .out(adder_1_out));  // open: cin, cout
  assign controlled_buffer_9_out = not_4_out ? PC_q : 32'bz;  // Controlled_Buffer controlled_buffer_10
  assign controlled_buffer_2_out = and_5_out ? controlled_buffer_9_out : 32'bz;  // Controlled_Buffer controlled_buffer_11
  Counter #(.max('h3), .width(2)) counter_1 (
    .clr(or_2_out), .load(1'b0), .up(1'b1), .count(1'b1), .clk(clk), .carry(counter_1_carry), .Q(counter_1_q));  // open: D
  and and_5 (and_5_out, counter_1_carry, comparator_2_lt);
  Bit_Extender #(.in_width(32), .out_width(8), .\type ("zero")) bit_extender_1 (
    .in({controlled_buffer_9_out[31:2], counter_1_q}), .out(bit_extender_1_out));
  ROM Init_firmware (.addr(bit_extender_1_out), .data(Init_firmware_data));
  not not_4 (not_4_out, comparator_2_lt);
  Comparator #(.mode("unsigned"), .width(2)) comparator_1 (
    .a(2'b00), .b(counter_1_q), .eq(comparator_1_eq));  // open: gt, lt
  Register #(.trigger("falling"), .width(32)) Instruction (
    .D(shift_register_1_p6), .en(comparator_1_eq), .clk(clk), .Q(instr));  // open: clr
  // Shift_Register #(.length(4), .width(8)) shift_register_1: pin names not known; wires that end beside it: or_2_out, 1'b0, 1'b1, clk, Init_firmware_data, shift_register_1_p6[7:0], shift_register_1_p6[15:8], shift_register_1_p6[23:16], shift_register_1_p6[31:24]
  Comparator #(.mode("unsigned"), .width(32)) comparator_2 (
    .a({32{1'b0}}), .b(instr), .lt(comparator_2_lt));  // open: gt, eq

  // Notes on the sheet:
  //   init-vector
  //   programs load 8 bits at a time, but data/address width is 32 bits = 4 cycles per instruction
  //   WARNING: PC increments 1 cycle before updating instruction register!
  //   instruction_address_misaligned
  //   to branch: pc_data, then incr_enable, then write_enable
  //   contents of Init_firmware (hex, n*v repeats v):
  //   0 0 10 b7 23 0 81 67 18 ba 58 37 10 2 48 37 72 e6 e2 37 5a 7e f4 17 58 73 e7 37 7c 2c c6 37 d6 8c 73
  //   37 b9 c9 c2 37 7e 22 94 37 43 42 d9 37 1c 6d bd 37 9c 68 5b 37 0 e 97 37 6e 76 97 37 9c 91 57 37 30
  //   50 d 37 bf 21 e8 37 4e c8 7 37 3 77 3f 37 e7 8a 94 37 3 9c 68 37 3d 26 3e 27 d2 83 1c 85 e4 2e 26 5d
  //   da 52 b6 24 3f 9f 90 8f 88 8 e8 8a 6c 94 48 f5 8f 4a a0 db d6 c5 ca 68 5a 3d f1 95 bb 81 75 2e 24 c1
  //   4a 98 90 9a a3 74 90 db 76 5f f7 35 f7 4e 22 ce 6d 6d a 90 d8 83 d6 2f 6f f8 14 94 75 65 21 38 46 85
  //   8a 7c a2 62 30 dc 29 17 e6 e9 c c6 cc 37 2c e6 5e 8d 79 3a 4f a4 cf 63 bd e4 2 56 57 2b d3 75 a0 97
  //   51 68 71 de c 77 37 d8 72 2a a6 92 b6 74 17 50 c8 d0 2b 87 5a 85 3c 6d 63 2c 8d b9 34 12 4b 51 ef 1f
  //   9a 9 ae c4 38 33 42 d7 fc f1 54 d5 9 e5 a4 81
endmodule

module execution_block (
  input  clk,
  input  rst,
  input  [19:0] imm,
  input  [31:0] rs1,
  input  [31:0] pc_data,
  input  [6:0] funct7,
  input  [31:0] rs2,
  input  [31:0] data_bus_in,
  input  [2:0] funct3,
  input  [6:0] opcode,
  output [31:0] rd,
  output read_pc_next,
  output addr_write,
  output addr_read,
  output [31:0] data_bus_out,
  output [31:0] address_out,
  output write_pc,
  output incr_pc
);

  wire and_1_out, and_2_out, and_3_out, and_4_out, and_5_out, and_6_out, and_7_out, and_10_out, and_11_out,
       and_12_out, and_13_out, and_14_out, AUIPC_out, comparator_1_eq, comparator_2_eq, comparator_3_eq,
       comparator_4_eq, comparator_5_eq, comparator_6_eq, comparator_7_eq, comparator_8_eq, comparator_8_lt,
       controlled_buffer_18_out, controlled_buffer_20_out, decoder_1_out0, decoder_1_out1, decoder_1_out2,
       decoder_1_out3, decoder_1_out4, decoder_1_out5, decoder_1_out6, decoder_1_out7, LUI_out, nor_1_out,
       nor_2_out, nor_3_out, not_1_out, not_2_out, not_3_out, not_4_out, not_5_out, not_6_out, not_7_out,
       not_8_out, or_1_out, or_2_out, or_3_out, or_4_out, or_5_out, or_7_out, or_8_out, or_9_out, or_10_out,
       or_11_out, or_12_out, t_ff_1_q, t_ff_2_q, undriven_2;
  wire [0:0] comparator_10_lt, comparator_11_lt, controlled_buffer_48_out;
  wire [4:0] controlled_buffer_9_out, controlled_buffer_25_out, controlled_buffer_27_out,
       controlled_buffer_29_out;
  wire [6:0] controlled_buffer_1_out;
  wire [31:0] adder_1_out, and_15_out, bit_extender_1_out, controlled_buffer_3_out, controlled_buffer_5_out,
       controlled_buffer_7_out, controlled_buffer_14_out, controlled_buffer_15_out, controlled_buffer_16_out,
       controlled_buffer_17_out, controlled_buffer_22_out, controlled_buffer_24_out,
       controlled_buffer_26_out, controlled_buffer_28_out, controlled_buffer_30_out,
       controlled_buffer_31_out, controlled_buffer_33_out, controlled_buffer_34_out,
       controlled_buffer_35_out, controlled_buffer_36_out, controlled_buffer_37_out,
       controlled_buffer_38_out, controlled_buffer_39_out, controlled_buffer_40_out,
       controlled_buffer_41_out, controlled_buffer_42_out, controlled_buffer_43_out,
       controlled_buffer_44_out, controlled_buffer_45_out, controlled_buffer_46_out,
       controlled_buffer_47_out, controlled_buffer_56_out, controlled_buffer_58_out, divider_1_out,
       multiplier_1_out, negator_1_out, or_13_out, shifter_1_out, shifter_2_out, shifter_3_out, undriven,
       undriven_3, xor_1_out;
  wire [31:1] controlled_buffer_48_out_2;
  wire [31:5] controlled_buffer_9_out_2;

  T_Flip_Flop t_ff_1 (.T(clk), .clk(clk), .Q(t_ff_1_q), .reset(rst));  // open: Qn, preset
  T_Flip_Flop t_ff_2 (.T(t_ff_1_q), .clk(clk), .Q(t_ff_2_q), .reset(rst));  // open: Qn, preset
  Comparator #(.mode("unsigned"), .width(5)) comparator_1 (
    .a(opcode[4:0]), .b(5'b10111), .eq(comparator_1_eq));  // open: gt, lt
  Comparator #(.mode("unsigned"), .width(7)) comparator_2 (
    .a(7'b1101111), .b(opcode), .eq(comparator_2_eq));  // open: gt, lt
  Comparator #(.mode("unsigned"), .width(7)) comparator_3 (
    .a(opcode), .b(7'b1100111), .eq(comparator_3_eq));  // open: gt, lt
  Comparator #(.mode("unsigned"), .width(7)) comparator_4 (
    .a(opcode), .b(7'b1100011), .eq(comparator_4_eq));  // open: gt, lt
  Comparator #(.mode("unsigned"), .width(5)) comparator_5 (
    .a(opcode[4:0]), .b(5'b10011), .eq(comparator_5_eq));  // open: gt, lt
  Comparator #(.mode("unsigned"), .width(5)) comparator_6 (
    .a(opcode[4:0]), .b(5'b10001), .eq(comparator_6_eq));  // open: gt, lt
  Comparator #(.mode("unsigned"), .width(3)) comparator_7 (
    .a(funct3), .b(3'b000), .eq(comparator_7_eq));  // open: gt, lt
  and and_1 (and_1_out, ~opcode[6], comparator_5_eq);  // AND_Gate
  and LUI (LUI_out, opcode[5], comparator_1_eq);
  and AUIPC (AUIPC_out, ~opcode[5], comparator_1_eq);  // AND_Gate
  and and_2 (and_2_out, comparator_7_eq, comparator_3_eq);
  not not_1 (not_1_out, and_7_out);
  assign controlled_buffer_1_out = not_1_out ? funct7 : 7'bz;  // Controlled_Buffer controlled_buffer_1
  and and_3 (and_3_out, ~t_ff_2_q, comparator_2_eq);  // AND_Gate
  and and_4 (and_4_out, t_ff_2_q, comparator_2_eq);
  and and_5 (and_5_out, ~t_ff_2_q, and_2_out);  // AND_Gate
  and and_6 (and_6_out, t_ff_2_q, and_2_out);
  and and_7 (and_7_out, and_1_out, ~opcode[5]);  // AND_Gate
  and and_8 (addr_read, comparator_6_eq, opcode[5]);
  and and_9 (addr_write, comparator_6_eq, ~opcode[5]);  // AND_Gate
  assign controlled_buffer_1_out = and_7_out ? imm[11:5] : 7'bz;  // Controlled_Buffer controlled_buffer_2
  assign bit_extender_1_out = {{20{imm[11]}}, imm[11:0]};  // Bit_Extender bit_extender_1
  assign controlled_buffer_3_out = or_1_out ? {{12{1'b0}}, imm} : 32'bz;  // Controlled_Buffer controlled_buffer_3
  not not_2 (not_2_out, or_1_out);
  or or_1 (or_1_out, LUI_out, AUIPC_out, and_7_out, addr_read, addr_write);
  assign controlled_buffer_3_out = not_2_out ? bit_extender_1_out : 32'bz;  // Controlled_Buffer controlled_buffer_4
  nor nor_1 (nor_1_out, or_2_out, or_3_out);
  or or_2 (or_2_out, and_10_out, and_4_out);
  assign controlled_buffer_5_out = or_3_out ? {controlled_buffer_3_out[19:0], {12{1'b0}}} : 32'bz;  // Controlled_Buffer controlled_buffer_5
  assign controlled_buffer_5_out = or_2_out ? {controlled_buffer_3_out[30:0], 1'b0} : 32'bz;  // Controlled_Buffer controlled_buffer_6
  assign controlled_buffer_7_out = or_4_out ? controlled_buffer_5_out : 32'bz;  // Controlled_Buffer controlled_buffer_7
  assign controlled_buffer_5_out = nor_1_out ? controlled_buffer_3_out : 32'bz;  // Controlled_Buffer controlled_buffer_8
  or or_3 (or_3_out, LUI_out, AUIPC_out);
  or or_4 (or_4_out, AUIPC_out, LUI_out);
  assign {controlled_buffer_9_out_2, controlled_buffer_9_out} = or_5_out ? controlled_buffer_5_out : 32'bz;  // Controlled_Buffer controlled_buffer_9
  or or_5 (or_5_out, and_7_out, and_6_out, addr_read, addr_write);
  assign {controlled_buffer_9_out_2, controlled_buffer_9_out} = or_8_out ? pc_data : 32'bz;  // Controlled_Buffer controlled_buffer_10
  assign controlled_buffer_7_out = or_7_out ? pc_data : 32'bz;  // Controlled_Buffer controlled_buffer_11
  or or_6 (read_pc_next, and_5_out, and_3_out);
  or or_7 (or_7_out, and_3_out, and_4_out, and_5_out);
  nor nor_2 (nor_2_out, or_8_out, addr_write, or_5_out);
  nor nor_3 (nor_3_out, or_7_out, or_4_out);
  buf or_8 (or_8_out, AUIPC_out);  // OR_Gate
  assign {controlled_buffer_9_out_2, controlled_buffer_9_out} = nor_2_out ? rs2 : 32'bz;  // Controlled_Buffer controlled_buffer_12
  not not_3 (not_3_out, funct3[1]);
  assign controlled_buffer_7_out = nor_3_out ? rs1 : 32'bz;  // Controlled_Buffer controlled_buffer_13
  assign controlled_buffer_14_out = not_3_out ? rs1 : 32'bz;  // Controlled_Buffer controlled_buffer_14
  assign controlled_buffer_15_out = not_3_out ? rs2 : 32'bz;  // Controlled_Buffer controlled_buffer_15
  assign controlled_buffer_16_out = funct3[1] ? rs1 : 32'bz;  // Controlled_Buffer controlled_buffer_16
  assign controlled_buffer_17_out = funct3[1] ? rs2 : 32'bz;  // Controlled_Buffer controlled_buffer_17
  Comparator #(.width(32)) comparator_8 (
    .a(controlled_buffer_14_out), .b(controlled_buffer_15_out), .eq(comparator_8_eq), .lt(comparator_8_lt));  // open: gt
  Comparator #(.mode("unsigned"), .width(32)) comparator_9 (
    .a(controlled_buffer_16_out), .b(controlled_buffer_17_out), .eq(comparator_8_eq), .lt(comparator_8_lt));  // open: gt
  assign controlled_buffer_18_out = funct3[2] ? comparator_8_lt : 1'bz;  // Controlled_Buffer controlled_buffer_18
  not not_4 (not_4_out, funct3[2]);
  assign controlled_buffer_18_out = not_4_out ? comparator_8_eq : 1'bz;  // Controlled_Buffer controlled_buffer_19
  not not_5 (not_5_out, controlled_buffer_18_out);
  assign controlled_buffer_20_out = not_6_out ? controlled_buffer_18_out : 1'bz;  // Controlled_Buffer controlled_buffer_20
  assign controlled_buffer_20_out = funct3[0] ? not_5_out : 1'bz;  // Controlled_Buffer controlled_buffer_21
  not not_6 (not_6_out, funct3[0]);
  assign controlled_buffer_22_out = addr_read ? data_bus_in : 32'bz;  // Controlled_Buffer controlled_buffer_22
  and and_10 (and_10_out, controlled_buffer_20_out, comparator_4_eq);
  Decoder #(.select(3)) decoder_1 (
    .out0(decoder_1_out0), .out1(decoder_1_out1), .out2(decoder_1_out2), .out3(decoder_1_out3),
    .out4(decoder_1_out4), .out5(decoder_1_out5), .out6(decoder_1_out6), .out7(decoder_1_out7), .sel(funct3),
    .en(and_1_out));
  assign data_bus_out = addr_write ? rs2 : 32'bz;  // Controlled_Buffer controlled_buffer_23
  or or_9 (or_9_out, and_3_out, and_10_out, and_4_out, LUI_out, AUIPC_out, and_5_out);
  and and_11 (and_11_out, decoder_1_out5, ~controlled_buffer_1_out[5]);  // AND_Gate
  and and_12 (and_12_out, controlled_buffer_1_out[5], decoder_1_out5);
  and and_13 (and_13_out, ~controlled_buffer_1_out[5], decoder_1_out0);  // AND_Gate
  and and_14 (and_14_out, controlled_buffer_1_out[5], decoder_1_out0);
  or or_10 (or_10_out, addr_read, and_6_out, and_13_out, addr_write);
  assign controlled_buffer_24_out = decoder_1_out1 ? controlled_buffer_7_out : 32'bz;  // Controlled_Buffer controlled_buffer_24
  assign controlled_buffer_25_out = decoder_1_out1 ? controlled_buffer_9_out : 5'bz;  // Controlled_Buffer controlled_buffer_25
  assign controlled_buffer_26_out = and_11_out ? controlled_buffer_7_out : 32'bz;  // Controlled_Buffer controlled_buffer_26
  assign controlled_buffer_27_out = and_11_out ? controlled_buffer_9_out : 5'bz;  // Controlled_Buffer controlled_buffer_27
  assign controlled_buffer_28_out = and_12_out ? controlled_buffer_7_out : 32'bz;  // Controlled_Buffer controlled_buffer_28
  assign controlled_buffer_29_out = and_12_out ? controlled_buffer_9_out : 5'bz;  // Controlled_Buffer controlled_buffer_29
  assign controlled_buffer_30_out = or_10_out ? controlled_buffer_7_out : 32'bz;  // Controlled_Buffer controlled_buffer_30
  assign controlled_buffer_31_out = or_10_out ? {controlled_buffer_9_out_2, controlled_buffer_9_out} : 32'bz;  // Controlled_Buffer controlled_buffer_31
  assign controlled_buffer_30_out = and_14_out ? controlled_buffer_7_out : 32'bz;  // Controlled_Buffer controlled_buffer_32
  assign controlled_buffer_33_out = and_14_out ? {controlled_buffer_9_out_2, controlled_buffer_9_out} : 32'bz;  // Controlled_Buffer controlled_buffer_33
  assign controlled_buffer_34_out = decoder_1_out7 ? controlled_buffer_7_out : 32'bz;  // Controlled_Buffer controlled_buffer_34
  assign controlled_buffer_35_out = decoder_1_out7 ? {controlled_buffer_9_out_2, controlled_buffer_9_out} : 32'bz;  // Controlled_Buffer controlled_buffer_35
  assign controlled_buffer_36_out = decoder_1_out4 ? controlled_buffer_7_out : 32'bz;  // Controlled_Buffer controlled_buffer_36
  assign controlled_buffer_37_out = decoder_1_out4 ? {controlled_buffer_9_out_2, controlled_buffer_9_out} : 32'bz;  // Controlled_Buffer controlled_buffer_37
  assign controlled_buffer_38_out = decoder_1_out6 ? controlled_buffer_7_out : 32'bz;  // Controlled_Buffer controlled_buffer_38
  assign controlled_buffer_39_out = decoder_1_out6 ? {controlled_buffer_9_out_2, controlled_buffer_9_out} : 32'bz;  // Controlled_Buffer controlled_buffer_39
  assign controlled_buffer_40_out = decoder_1_out2 ? controlled_buffer_7_out : 32'bz;  // Controlled_Buffer controlled_buffer_40
  assign controlled_buffer_41_out = decoder_1_out2 ? {controlled_buffer_9_out_2, controlled_buffer_9_out} : 32'bz;  // Controlled_Buffer controlled_buffer_41
  assign controlled_buffer_42_out = decoder_1_out3 ? controlled_buffer_7_out : 32'bz;  // Controlled_Buffer controlled_buffer_42
  assign controlled_buffer_43_out = decoder_1_out3 ? {controlled_buffer_9_out_2, controlled_buffer_9_out} : 32'bz;  // Controlled_Buffer controlled_buffer_43
  assign controlled_buffer_44_out = undriven_2 ? undriven_3 : 32'bz;  // Controlled_Buffer controlled_buffer_44
  assign controlled_buffer_45_out = undriven_2 ? undriven : 32'bz;  // Controlled_Buffer controlled_buffer_45
  assign controlled_buffer_46_out = undriven_2 ? undriven_3 : 32'bz;  // Controlled_Buffer controlled_buffer_46
  assign controlled_buffer_47_out = undriven_2 ? undriven : 32'bz;  // Controlled_Buffer controlled_buffer_47
  or or_11 (or_11_out, addr_read, addr_write);
  assign {controlled_buffer_48_out_2, controlled_buffer_48_out[0]} = or_9_out ? controlled_buffer_7_out : 32'bz;  // Controlled_Buffer controlled_buffer_48
  assign {controlled_buffer_48_out_2, controlled_buffer_48_out[0]} = decoder_1_out1 ? shifter_1_out : 32'bz;  // Controlled_Buffer controlled_buffer_49
  Shifter #(.width(32)) shifter_1 (
    .in(controlled_buffer_24_out), .\dist (controlled_buffer_25_out), .out(shifter_1_out));
  assign {controlled_buffer_48_out_2, controlled_buffer_48_out[0]} = and_11_out ? shifter_2_out : 32'bz;  // Controlled_Buffer controlled_buffer_50
  Shifter #(.shift("lr"), .width(32)) shifter_2 (
    .in(controlled_buffer_26_out), .\dist (controlled_buffer_27_out), .out(shifter_2_out));
  assign {controlled_buffer_48_out_2, controlled_buffer_48_out[0]} = and_12_out ? shifter_3_out : 32'bz;  // Controlled_Buffer controlled_buffer_51
  Shifter #(.shift("ar"), .width(32)) shifter_3 (
    .in(controlled_buffer_28_out), .\dist (controlled_buffer_29_out), .out(shifter_3_out));
  or or_12 (or_12_out, or_10_out, and_14_out);
  assign controlled_buffer_31_out = and_14_out ? negator_1_out : 32'bz;  // Controlled_Buffer controlled_buffer_52
  Negator #(.width(32)) negator_1 (.in(controlled_buffer_33_out), .out(negator_1_out));
  assign and_15_out = controlled_buffer_34_out & controlled_buffer_35_out;  // AND_Gate and_15, 32 bits wide
  assign {controlled_buffer_48_out_2, controlled_buffer_48_out[0]} = decoder_1_out7 ? and_15_out : 32'bz;  // Controlled_Buffer controlled_buffer_53
  assign xor_1_out = controlled_buffer_36_out ^ controlled_buffer_37_out;  // XOR_Gate xor_1, 32 bits wide
  assign {controlled_buffer_48_out_2, controlled_buffer_48_out[0]} = decoder_1_out4 ? xor_1_out : 32'bz;  // Controlled_Buffer controlled_buffer_54
  assign or_13_out = controlled_buffer_38_out | controlled_buffer_39_out;  // OR_Gate or_13, 32 bits wide
  assign {controlled_buffer_48_out_2, controlled_buffer_48_out[0]} = decoder_1_out6 ? or_13_out : 32'bz;  // Controlled_Buffer controlled_buffer_55
  Comparator #(.width(32)) comparator_10 (
    .a(controlled_buffer_40_out), .b(controlled_buffer_41_out), .lt(comparator_10_lt[0]));  // open: gt, eq
  Comparator #(.mode("unsigned"), .width(32)) comparator_11 (
    .a(controlled_buffer_42_out), .b(controlled_buffer_43_out), .lt(comparator_11_lt[0]));  // open: gt, eq
  assign controlled_buffer_56_out = undriven_2 ? multiplier_1_out : 32'bz;  // Controlled_Buffer controlled_buffer_56
  Multiplier #(.width(32)) multiplier_1 (
    .a(controlled_buffer_44_out), .b(controlled_buffer_45_out), .out(multiplier_1_out));  // open: cin, cout
  assign controlled_buffer_56_out = undriven_2 ? divider_1_out : 32'bz;  // Controlled_Buffer controlled_buffer_57
  Divider #(.width(32)) divider_1 (
    .a(controlled_buffer_46_out), .b(controlled_buffer_47_out), .out(divider_1_out));  // open: upper, rem
  assign controlled_buffer_58_out = and_6_out ? {controlled_buffer_48_out_2, 1'b0} : 32'bz;  // Controlled_Buffer controlled_buffer_58
  not not_7 (not_7_out, and_6_out);
  assign {controlled_buffer_48_out_2, controlled_buffer_48_out[0]} = or_12_out ? adder_1_out : 32'bz;  // Controlled_Buffer controlled_buffer_59
  Adder #(.width(32)) adder_1 (
    .a(controlled_buffer_30_out), .b(controlled_buffer_31_out), .out(adder_1_out));  // open: cin, cout
  assign {controlled_buffer_48_out_2, controlled_buffer_48_out[0]} = decoder_1_out2 ? {{31{1'b1}}, comparator_10_lt[0]} : 32'bz;  // Controlled_Buffer controlled_buffer_60
  assign {controlled_buffer_48_out_2, controlled_buffer_48_out[0]} = decoder_1_out3 ? {{31{1'b1}}, comparator_11_lt[0]} : 32'bz;  // Controlled_Buffer controlled_buffer_61
  assign controlled_buffer_58_out = not_7_out ? {controlled_buffer_48_out_2, controlled_buffer_48_out[0]} : 32'bz;  // Controlled_Buffer controlled_buffer_62
  or or_14 (incr_pc, and_10_out, and_4_out);
  assign rd = addr_read ? controlled_buffer_22_out : 32'bz;  // Controlled_Buffer controlled_buffer_63
  not not_8 (not_8_out, addr_read);
  or or_15 (write_pc, and_6_out, incr_pc);
  assign rd = not_8_out ? controlled_buffer_58_out : 32'bz;  // Controlled_Buffer controlled_buffer_64
  assign address_out = or_11_out ? controlled_buffer_58_out : 32'bz;  // Controlled_Buffer controlled_buffer_65

  // Notes on the sheet:
  //   pc_data: pull=down
  //   Integer math
  //   JAL
  //   Branch
  //   store?
  //   fix for I-types using func7 + 5 bit imm
  //   JALR
  //   use rs2
  //   Lx
  //   Sx
  //   imm20 : imm12
  //   Immediate value logic
  //   < lsh1 lsh12 >
  //   < A B >
  //   < A B >
  //   Input B
  //   Input A
  //   branch!
  //   Branch logic
  //   store
  //   load
  //   sll
  //   srl
  //   sra
  //   multiply
  //   RV32M
  //   divide
  //   add
  //   subtract
  //   and
  //   xor
  //   or
  //   slt
  //   sltu
  //   unset lsb
endmodule

// clock divider
module por_block (
  input  clk,
  input  rst_btn,
  output rst
);

  wire and_1_out, t_ff_1_q, t_ff_2_q, t_ff_3_q;

  T_Flip_Flop t_ff_1 (.T(rst), .clk(clk), .Q(t_ff_1_q), .reset(rst_btn), .preset(1'b0));  // open: Qn
  T_Flip_Flop t_ff_2 (.T(t_ff_1_q), .clk(clk), .Q(t_ff_2_q), .reset(rst_btn), .preset(1'b0));  // open: Qn
  S_R_Flip_Flop #(.trigger("falling")) System_reset_latch (
    .S(1'b0), .R(t_ff_3_q), .clk(clk), .Q(rst), .reset(1'b0), .preset(rst_btn));  // open: Qn
  and and_1 (and_1_out, t_ff_1_q, t_ff_2_q);
  T_Flip_Flop t_ff_3 (.T(and_1_out), .clk(clk), .Q(t_ff_3_q), .reset(rst_btn), .preset(1'b0));  // open: Qn
endmodule

module register_block_no_transistors (
  input  [31:0] rd,
  input  [4:0] rs1_sel,
  input  clk,
  input  [4:0] rs2_sel,
  input  [4:0] rd_sel,
  input  rst,
  output [31:0] rs1,
  output [31:0] rs2
);

  wire pull_resistor_1_node, pull_resistor_2_node, pull_resistor_3_node;
  wire [31:0] x1_q, x2_q, x3_q, x4_q, x5_q, x6_q, x7_q, x8_q, x9_q, x10_q, x11_q, x12_q, x13_q, x14_q, x15_q,
       x16_q, x17_q, x18_q, x19_q, x20_q, x21_q, x22_q, x23_q, x24_q, x25_q, x26_q, x27_q, x28_q, x29_q,
       x30_q, x31_q;
  wire [34:32] decoder_3_out0, decoder_3_out1, decoder_3_out2, decoder_3_out3, decoder_3_out4,
       decoder_3_out5, decoder_3_out6, decoder_3_out7, decoder_3_out8, decoder_3_out9, decoder_3_out10,
       decoder_3_out11, decoder_3_out12, decoder_3_out13, decoder_3_out14, decoder_3_out15, decoder_3_out16,
       decoder_3_out17, decoder_3_out18, decoder_3_out19, decoder_3_out20, decoder_3_out21, decoder_3_out22,
       decoder_3_out23, decoder_3_out24, decoder_3_out25, decoder_3_out26, decoder_3_out27, decoder_3_out28,
       decoder_3_out29, decoder_3_out30, decoder_3_out31;

  assign rs1 = decoder_3_out7[32] ? x7_q : 32'bz;  // Controlled_Buffer controlled_buffer_1
  Register #(.width(32)) x7 (.D(rd), .en(decoder_3_out7[34]), .clk(clk), .Q(x7_q), .clr(rst));
  assign rs1 = decoder_3_out15[32] ? x15_q : 32'bz;  // Controlled_Buffer controlled_buffer_2
  Register #(.width(32)) x15 (.D(rd), .en(decoder_3_out15[34]), .clk(clk), .Q(x15_q), .clr(rst));
  assign rs1 = decoder_3_out23[32] ? x23_q : 32'bz;  // Controlled_Buffer controlled_buffer_3
  Register #(.width(32)) x23 (.D(rd), .en(decoder_3_out23[34]), .clk(clk), .Q(x23_q), .clr(rst));
  assign rs1 = decoder_3_out31[32] ? x31_q : 32'bz;  // Controlled_Buffer controlled_buffer_4
  Register #(.width(32)) x31 (.D(rd), .en(decoder_3_out31[34]), .clk(clk), .Q(x31_q), .clr(rst));
  assign rs1 = decoder_3_out6[32] ? x6_q : 32'bz;  // Controlled_Buffer controlled_buffer_5
  assign rs2 = decoder_3_out7[33] ? x7_q : 32'bz;  // Controlled_Buffer controlled_buffer_6
  Register #(.width(32)) x6 (.D(rd), .en(decoder_3_out6[34]), .clk(clk), .Q(x6_q), .clr(rst));
  assign rs1 = decoder_3_out14[32] ? x14_q : 32'bz;  // Controlled_Buffer controlled_buffer_7
  assign rs2 = decoder_3_out15[33] ? x15_q : 32'bz;  // Controlled_Buffer controlled_buffer_8
  Register #(.width(32)) x14 (.D(rd), .en(decoder_3_out14[34]), .clk(clk), .Q(x14_q), .clr(rst));
  assign rs1 = decoder_3_out22[32] ? x22_q : 32'bz;  // Controlled_Buffer controlled_buffer_9
  assign rs2 = decoder_3_out23[33] ? x23_q : 32'bz;  // Controlled_Buffer controlled_buffer_10
  Register #(.width(32)) x22 (.D(rd), .en(decoder_3_out22[34]), .clk(clk), .Q(x22_q), .clr(rst));
  assign rs1 = decoder_3_out30[32] ? x30_q : 32'bz;  // Controlled_Buffer controlled_buffer_11
  assign rs2 = decoder_3_out31[33] ? x31_q : 32'bz;  // Controlled_Buffer controlled_buffer_12
  Register #(.width(32)) x30 (.D(rd), .en(decoder_3_out30[34]), .clk(clk), .Q(x30_q), .clr(rst));
  assign rs1 = decoder_3_out5[32] ? x5_q : 32'bz;  // Controlled_Buffer controlled_buffer_13
  assign rs2 = decoder_3_out6[33] ? x6_q : 32'bz;  // Controlled_Buffer controlled_buffer_14
  Register #(.width(32)) x5 (.D(rd), .en(decoder_3_out5[34]), .clk(clk), .Q(x5_q), .clr(rst));
  assign rs1 = decoder_3_out13[32] ? x13_q : 32'bz;  // Controlled_Buffer controlled_buffer_15
  assign rs2 = decoder_3_out14[33] ? x14_q : 32'bz;  // Controlled_Buffer controlled_buffer_16
  Register #(.width(32)) x13 (.D(rd), .en(decoder_3_out13[34]), .clk(clk), .Q(x13_q), .clr(rst));
  assign rs1 = decoder_3_out21[32] ? x21_q : 32'bz;  // Controlled_Buffer controlled_buffer_17
  assign rs2 = decoder_3_out22[33] ? x22_q : 32'bz;  // Controlled_Buffer controlled_buffer_18
  Register #(.width(32)) x21 (.D(rd), .en(decoder_3_out21[34]), .clk(clk), .Q(x21_q), .clr(rst));
  assign rs1 = decoder_3_out29[32] ? x29_q : 32'bz;  // Controlled_Buffer controlled_buffer_19
  assign rs2 = decoder_3_out30[33] ? x30_q : 32'bz;  // Controlled_Buffer controlled_buffer_20
  Register #(.width(32)) x29 (.D(rd), .en(decoder_3_out29[34]), .clk(clk), .Q(x29_q), .clr(rst));
  assign rs1 = decoder_3_out4[32] ? x4_q : 32'bz;  // Controlled_Buffer controlled_buffer_21
  assign rs2 = decoder_3_out5[33] ? x5_q : 32'bz;  // Controlled_Buffer controlled_buffer_22
  Register #(.width(32)) x4 (.D(rd), .en(decoder_3_out4[34]), .clk(clk), .Q(x4_q), .clr(rst));
  assign rs1 = decoder_3_out12[32] ? x12_q : 32'bz;  // Controlled_Buffer controlled_buffer_23
  assign rs2 = decoder_3_out13[33] ? x13_q : 32'bz;  // Controlled_Buffer controlled_buffer_24
  Register #(.width(32)) x12 (.D(rd), .en(decoder_3_out12[34]), .clk(clk), .Q(x12_q), .clr(rst));
  assign rs1 = decoder_3_out20[32] ? x20_q : 32'bz;  // Controlled_Buffer controlled_buffer_25
  assign rs2 = decoder_3_out21[33] ? x21_q : 32'bz;  // Controlled_Buffer controlled_buffer_26
  Register #(.width(32)) x20 (.D(rd), .en(decoder_3_out20[34]), .clk(clk), .Q(x20_q), .clr(rst));
  assign rs1 = decoder_3_out28[32] ? x28_q : 32'bz;  // Controlled_Buffer controlled_buffer_27
  assign rs2 = decoder_3_out29[33] ? x29_q : 32'bz;  // Controlled_Buffer controlled_buffer_28
  Register #(.width(32)) x28 (.D(rd), .en(decoder_3_out28[34]), .clk(clk), .Q(x28_q), .clr(rst));
  assign rs1 = decoder_3_out3[32] ? x3_q : 32'bz;  // Controlled_Buffer controlled_buffer_29
  assign rs2 = decoder_3_out4[33] ? x4_q : 32'bz;  // Controlled_Buffer controlled_buffer_30
  Register #(.width(32)) x3 (.D(rd), .en(decoder_3_out3[34]), .clk(clk), .Q(x3_q), .clr(rst));
  assign rs1 = decoder_3_out11[32] ? x11_q : 32'bz;  // Controlled_Buffer controlled_buffer_31
  assign rs2 = decoder_3_out12[33] ? x12_q : 32'bz;  // Controlled_Buffer controlled_buffer_32
  Register #(.width(32)) x11 (.D(rd), .en(decoder_3_out11[34]), .clk(clk), .Q(x11_q), .clr(rst));
  assign rs1 = decoder_3_out19[32] ? x19_q : 32'bz;  // Controlled_Buffer controlled_buffer_33
  assign rs2 = decoder_3_out20[33] ? x20_q : 32'bz;  // Controlled_Buffer controlled_buffer_34
  Register #(.width(32)) x19 (.D(rd), .en(decoder_3_out19[34]), .clk(clk), .Q(x19_q), .clr(rst));
  assign rs1 = decoder_3_out27[32] ? x27_q : 32'bz;  // Controlled_Buffer controlled_buffer_35
  assign rs2 = decoder_3_out28[33] ? x28_q : 32'bz;  // Controlled_Buffer controlled_buffer_36
  Register #(.width(32)) x27 (.D(rd), .en(decoder_3_out27[34]), .clk(clk), .Q(x27_q), .clr(rst));
  assign rs1 = decoder_3_out2[32] ? x2_q : 32'bz;  // Controlled_Buffer controlled_buffer_37
  assign rs2 = decoder_3_out3[33] ? x3_q : 32'bz;  // Controlled_Buffer controlled_buffer_38
  Register #(.width(32)) x2 (.D(rd), .en(decoder_3_out2[34]), .clk(clk), .Q(x2_q), .clr(rst));
  assign rs1 = decoder_3_out10[32] ? x10_q : 32'bz;  // Controlled_Buffer controlled_buffer_39
  assign rs2 = decoder_3_out11[33] ? x11_q : 32'bz;  // Controlled_Buffer controlled_buffer_40
  Register #(.width(32)) x10 (.D(rd), .en(decoder_3_out10[34]), .clk(clk), .Q(x10_q), .clr(rst));
  assign rs1 = decoder_3_out18[32] ? x18_q : 32'bz;  // Controlled_Buffer controlled_buffer_41
  assign rs2 = decoder_3_out19[33] ? x19_q : 32'bz;  // Controlled_Buffer controlled_buffer_42
  Register #(.width(32)) x18 (.D(rd), .en(decoder_3_out18[34]), .clk(clk), .Q(x18_q), .clr(rst));
  assign rs1 = decoder_3_out26[32] ? x26_q : 32'bz;  // Controlled_Buffer controlled_buffer_43
  assign rs2 = decoder_3_out27[33] ? x27_q : 32'bz;  // Controlled_Buffer controlled_buffer_44
  Register #(.width(32)) x26 (.D(rd), .en(decoder_3_out26[34]), .clk(clk), .Q(x26_q), .clr(rst));
  assign rs1 = decoder_3_out1[32] ? x1_q : 32'bz;  // Controlled_Buffer controlled_buffer_45
  assign rs2 = decoder_3_out2[33] ? x2_q : 32'bz;  // Controlled_Buffer controlled_buffer_46
  Register #(.width(32)) x1 (.D(rd), .en(decoder_3_out1[34]), .clk(clk), .Q(x1_q), .clr(rst));
  assign rs1 = decoder_3_out9[32] ? x9_q : 32'bz;  // Controlled_Buffer controlled_buffer_47
  assign rs2 = decoder_3_out10[33] ? x10_q : 32'bz;  // Controlled_Buffer controlled_buffer_48
  Register #(.width(32)) x9 (.D(rd), .en(decoder_3_out9[34]), .clk(clk), .Q(x9_q), .clr(rst));
  assign rs1 = decoder_3_out17[32] ? x17_q : 32'bz;  // Controlled_Buffer controlled_buffer_49
  assign rs2 = decoder_3_out18[33] ? x18_q : 32'bz;  // Controlled_Buffer controlled_buffer_50
  Register #(.width(32)) x17 (.D(rd), .en(decoder_3_out17[34]), .clk(clk), .Q(x17_q), .clr(rst));
  assign rs1 = decoder_3_out25[32] ? x25_q : 32'bz;  // Controlled_Buffer controlled_buffer_51
  assign rs2 = decoder_3_out26[33] ? x26_q : 32'bz;  // Controlled_Buffer controlled_buffer_52
  Register #(.width(32)) x25 (.D(rd), .en(decoder_3_out25[34]), .clk(clk), .Q(x25_q), .clr(rst));
  assign rs1 = decoder_3_out0[32] ? {32{1'b0}} : 32'bz;  // Controlled_Buffer controlled_buffer_53
  assign rs2 = decoder_3_out1[33] ? x1_q : 32'bz;  // Controlled_Buffer controlled_buffer_54
  assign rs1 = decoder_3_out8[32] ? x8_q : 32'bz;  // Controlled_Buffer controlled_buffer_55
  assign rs2 = decoder_3_out9[33] ? x9_q : 32'bz;  // Controlled_Buffer controlled_buffer_56
  Register #(.width(32)) x8 (.D(rd), .en(decoder_3_out8[34]), .clk(clk), .Q(x8_q), .clr(rst));
  assign rs1 = decoder_3_out16[32] ? x16_q : 32'bz;  // Controlled_Buffer controlled_buffer_57
  assign rs2 = decoder_3_out17[33] ? x17_q : 32'bz;  // Controlled_Buffer controlled_buffer_58
  Register #(.width(32)) x16 (.D(rd), .en(decoder_3_out16[34]), .clk(clk), .Q(x16_q), .clr(rst));
  assign rs1 = decoder_3_out24[32] ? x24_q : 32'bz;  // Controlled_Buffer controlled_buffer_59
  assign rs2 = decoder_3_out25[33] ? x25_q : 32'bz;  // Controlled_Buffer controlled_buffer_60
  Register #(.width(32)) x24 (.D(rd), .en(decoder_3_out24[34]), .clk(clk), .Q(x24_q), .clr(rst));
  assign rs2 = decoder_3_out0[33] ? {32{1'b0}} : 32'bz;  // Controlled_Buffer controlled_buffer_61
  assign rs2 = decoder_3_out8[33] ? x8_q : 32'bz;  // Controlled_Buffer controlled_buffer_62
  assign rs2 = decoder_3_out16[33] ? x16_q : 32'bz;  // Controlled_Buffer controlled_buffer_63
  assign rs2 = decoder_3_out24[33] ? x24_q : 32'bz;  // Controlled_Buffer controlled_buffer_64
  Decoder #(.select(5)) decoder_1 (
    .out0(decoder_3_out0[32]), .out1(decoder_3_out1[32]), .out2(decoder_3_out2[32]),
    .out3(decoder_3_out3[32]), .out4(decoder_3_out4[32]), .out5(decoder_3_out5[32]),
    .out6(decoder_3_out6[32]), .out7(decoder_3_out7[32]), .out8(decoder_3_out8[32]),
    .out9(decoder_3_out9[32]), .out10(decoder_3_out10[32]), .out11(decoder_3_out11[32]),
    .out12(decoder_3_out12[32]), .out13(decoder_3_out13[32]), .out14(decoder_3_out14[32]),
    .out15(decoder_3_out15[32]), .out16(decoder_3_out16[32]), .out17(decoder_3_out17[32]),
    .out18(decoder_3_out18[32]), .out19(decoder_3_out19[32]), .out20(decoder_3_out20[32]),
    .out21(decoder_3_out21[32]), .out22(decoder_3_out22[32]), .out23(decoder_3_out23[32]),
    .out24(decoder_3_out24[32]), .out25(decoder_3_out25[32]), .out26(decoder_3_out26[32]),
    .out27(decoder_3_out27[32]), .out28(decoder_3_out28[32]), .out29(decoder_3_out29[32]),
    .out30(decoder_3_out30[32]), .out31(decoder_3_out31[32]), .sel(rs1_sel), .en(pull_resistor_1_node));
  Pull_Resistor #(.pull(1)) pull_resistor_1 (.node(pull_resistor_1_node));
  Decoder #(.select(5)) decoder_2 (
    .out0(decoder_3_out0[33]), .out1(decoder_3_out1[33]), .out2(decoder_3_out2[33]),
    .out3(decoder_3_out3[33]), .out4(decoder_3_out4[33]), .out5(decoder_3_out5[33]),
    .out6(decoder_3_out6[33]), .out7(decoder_3_out7[33]), .out8(decoder_3_out8[33]),
    .out9(decoder_3_out9[33]), .out10(decoder_3_out10[33]), .out11(decoder_3_out11[33]),
    .out12(decoder_3_out12[33]), .out13(decoder_3_out13[33]), .out14(decoder_3_out14[33]),
    .out15(decoder_3_out15[33]), .out16(decoder_3_out16[33]), .out17(decoder_3_out17[33]),
    .out18(decoder_3_out18[33]), .out19(decoder_3_out19[33]), .out20(decoder_3_out20[33]),
    .out21(decoder_3_out21[33]), .out22(decoder_3_out22[33]), .out23(decoder_3_out23[33]),
    .out24(decoder_3_out24[33]), .out25(decoder_3_out25[33]), .out26(decoder_3_out26[33]),
    .out27(decoder_3_out27[33]), .out28(decoder_3_out28[33]), .out29(decoder_3_out29[33]),
    .out30(decoder_3_out30[33]), .out31(decoder_3_out31[33]), .sel(rs2_sel), .en(pull_resistor_2_node));
  Pull_Resistor #(.pull(1)) pull_resistor_2 (.node(pull_resistor_2_node));
  Pull_Resistor #(.pull(1)) pull_resistor_3 (.node(pull_resistor_3_node));
  Decoder #(.select(5)) decoder_3 (
    .out0(decoder_3_out0[34]), .out1(decoder_3_out1[34]), .out2(decoder_3_out2[34]),
    .out3(decoder_3_out3[34]), .out4(decoder_3_out4[34]), .out5(decoder_3_out5[34]),
    .out6(decoder_3_out6[34]), .out7(decoder_3_out7[34]), .out8(decoder_3_out8[34]),
    .out9(decoder_3_out9[34]), .out10(decoder_3_out10[34]), .out11(decoder_3_out11[34]),
    .out12(decoder_3_out12[34]), .out13(decoder_3_out13[34]), .out14(decoder_3_out14[34]),
    .out15(decoder_3_out15[34]), .out16(decoder_3_out16[34]), .out17(decoder_3_out17[34]),
    .out18(decoder_3_out18[34]), .out19(decoder_3_out19[34]), .out20(decoder_3_out20[34]),
    .out21(decoder_3_out21[34]), .out22(decoder_3_out22[34]), .out23(decoder_3_out23[34]),
    .out24(decoder_3_out24[34]), .out25(decoder_3_out25[34]), .out26(decoder_3_out26[34]),
    .out27(decoder_3_out27[34]), .out28(decoder_3_out28[34]), .out29(decoder_3_out29[34]),
    .out30(decoder_3_out30[34]), .out31(decoder_3_out31[34]), .sel(rd_sel), .en(pull_resistor_3_node));

  // Notes on the sheet:
  //   x0
  //   rs1 decoder
  //   rs2 decoder
  //   rd decoder
endmodule

module mmu_block (
  input  [31:0] data_in,
  input  [31:0] address_in,
  input  clk,
  input  write,
  input  [2:0] funct3,
  input  read,
  input  rst,
  output [31:0] data_out,
  output busy
);

  wire and_1_out, and_2_out, and_3_out, and_4_out, and_5_out, and_6_out, and_7_out, and_8_out, and_9_out,
       comparator_1_eq, controlled_buffer_11_out, data_written_q, or_1_out, or_2_out, or_3_out, or_5_out,
       read_output_ready_q, read_output_written_q, read_received_q, s_r_ff_1_q, write_data_ready_q,
       write_received_q;
  wire [2:0] bit_extender_3_out;
  wire [4:0] counter_1_q, shifter_1_out;
  wire [5:0] bit_extender_1_out;
  wire [7:0] bit_extender_2_out, controlled_buffer_3_out, controlled_buffer_6_out, shift_register_1_p4,
       shift_register_1_p10, shift_register_1_p11, shift_register_1_p12;
  wire [15:0] shift_register_1_p9;

  S_R_Flip_Flop write_received (
    .S(write), .R(1'b0), .clk(clk), .Q(write_received_q), .reset(or_1_out), .preset(1'b0));  // open: Qn
  or or_1 (or_1_out, rst, s_r_ff_1_q, data_written_q);
  S_R_Flip_Flop read_received (
    .S(read), .R(1'b0), .clk(clk), .Q(read_received_q), .reset(or_1_out), .preset(1'b0));  // open: Qn
  Bit_Extender #(.in_width(32), .out_width(6)) bit_extender_1 (.in(address_in), .out(bit_extender_1_out));
  S_R_Flip_Flop #(.trigger("falling")) write_data_ready (
    .S(write_received_q), .R(1'b0), .clk(clk), .Q(write_data_ready_q), .reset(or_1_out), .preset(1'b0));  // open: Qn
  S_R_Flip_Flop read_output_ready (
    .S(read_received_q), .R(1'b0), .clk(clk), .Q(read_output_ready_q), .reset(or_1_out), .preset(1'b0));  // open: Qn
  S_R_Flip_Flop #(.trigger("falling")) data_written (
    .S(and_4_out), .R(data_written_q), .clk(clk), .Q(data_written_q), .reset(or_1_out), .preset(and_3_out));  // open: Qn
  or or_2 (or_2_out, read_output_ready_q, and_1_out);
  and and_1 (and_1_out, write_data_ready_q, write_received_q);
  and and_2 (and_2_out, ~write_data_ready_q, write_received_q);  // AND_Gate
  and and_3 (and_3_out, write_received_q, comparator_1_eq);
  and and_4 (and_4_out, comparator_1_eq, read_received_q);
  or or_3 (or_3_out, data_written_q, or_1_out);
  or or_4 (busy, read_output_ready_q, write_received_q);
  // Shift_Register #(.length(4), .trigger("falling"), .width(8)) shift_register_1: pin names not known; wires that end beside it: and_2_out, or_2_out, clk, shift_register_1_p4, 8'hc, 8'h9, 8'h6, 8'h3, shift_register_1_p9[7:0], shift_register_1_p10, shift_register_1_p11, shift_register_1_p12
  Counter #(.max('h1f), .width(5)) counter_1 (
    .clr(or_3_out), .load(1'b0), .up(1'b1), .count(busy), .clk(clk), .Q(counter_1_q));  // open: D, carry
  S_R_Flip_Flop #(.trigger("falling")) read_output_written (
    .S(comparator_1_eq), .R(or_1_out), .clk(clk), .Q(read_output_written_q));  // open: reset, Qn, preset
  S_R_Flip_Flop s_r_ff_1 (
    .S(read_output_written_q), .R(or_1_out), .clk(clk), .Q(s_r_ff_1_q));  // open: reset, Qn, preset
  and and_5 (and_5_out, write_data_ready_q, write_received_q);
  assign shift_register_1_p9[15:8] = or_5_out ? shift_register_1_p10 : 8'bz;  // Controlled_Buffer controlled_buffer_1
  assign shift_register_1_p9[15:8] = and_9_out ? {8{1'b0}} : 8'bz;  // Controlled_Buffer controlled_buffer_2
  assign controlled_buffer_3_out = shifter_1_out[2] ? shift_register_1_p11 : 8'bz;  // Controlled_Buffer controlled_buffer_3
  assign shift_register_1_p9[15:8] = and_8_out ? bit_extender_2_out : 8'bz;  // Controlled_Buffer controlled_buffer_4
  RAM ram_1 (
    .addr({bit_extender_1_out, counter_1_q[1:0]}), .we(and_5_out), .oe(read_received_q), .clk(clk),
    .din(shift_register_1_p12), .dout(shift_register_1_p4));
  assign controlled_buffer_3_out = and_6_out ? {8{1'b0}} : 8'bz;  // Controlled_Buffer controlled_buffer_5
  assign controlled_buffer_6_out = shifter_1_out[2] ? shift_register_1_p12 : 8'bz;  // Controlled_Buffer controlled_buffer_6
  assign controlled_buffer_3_out = and_7_out ? bit_extender_2_out : 8'bz;  // Controlled_Buffer controlled_buffer_7
  assign controlled_buffer_6_out = and_6_out ? {8{1'b0}} : 8'bz;  // Controlled_Buffer controlled_buffer_8
  assign controlled_buffer_6_out = and_7_out ? bit_extender_2_out : 8'bz;  // Controlled_Buffer controlled_buffer_9
  assign data_out = read_output_written_q ? {controlled_buffer_6_out, controlled_buffer_3_out, shift_register_1_p9} : 32'bz;  // Controlled_Buffer controlled_buffer_10
  // Probe on shift_register_1_p4
  assign controlled_buffer_11_out = shifter_1_out[1] ? shift_register_1_p10[7] : 1'bz;  // Controlled_Buffer controlled_buffer_11
  assign controlled_buffer_11_out = shifter_1_out[2] ? shift_register_1_p11[7] : 1'bz;  // Controlled_Buffer controlled_buffer_12
  assign controlled_buffer_11_out = shifter_1_out[0] ? shift_register_1_p9[7] : 1'bz;  // Controlled_Buffer controlled_buffer_13
  assign bit_extender_2_out = {{7{controlled_buffer_11_out}}, controlled_buffer_11_out};  // Bit_Extender bit_extender_2
  and and_6 (and_6_out, ~shifter_1_out[2], ~funct3[2]);  // AND_Gate
  and and_7 (and_7_out, ~shifter_1_out[2], funct3[2]);  // AND_Gate
  buf and_8 (and_8_out, funct3[2]);  // AND_Gate AND_Gate
  and and_9 (and_9_out, ~or_5_out, ~funct3[2]);  // AND_Gate
  or or_5 (or_5_out, shifter_1_out[2], shifter_1_out[1]);
  Comparator #(.mode("unsigned"), .width(5)) comparator_1 (
    .a(counter_1_q), .b(shifter_1_out), .eq(comparator_1_eq));  // open: gt, lt
  Shifter #(.width(5)) shifter_1 (.in(5'b00001), .\dist (bit_extender_3_out), .out(shifter_1_out));
  assign bit_extender_3_out = {{1{1'b0}}, funct3[1:0]};  // Bit_Extender bit_extender_3

  // Notes on the sheet:
  //   4+n cycles per read  of n bytes :(
  //   TODO: tighten timings using RISING/HIGH/FALLING/LOW
  //   unsigned?
endmodule
