// Logisim project video.circ as structural Verilog: 1 circuit, main circuit main
module main (
);

  wire clock_1_out, counter_1_carry, pull_resistor_1_node, pull_resistor_3_node;
  wire [7:0] counter_1_q, counter_1_q_2;
  wire [15:0] rgb_video_1_p3;

  Clock clock_1 (.out(clock_1_out));
  Counter #(.max('hffff), .width(16)) counter_1 (
    .count(pull_resistor_1_node), .clk(clock_1_out), .carry(counter_1_carry), .Q({counter_1_q_2, counter_1_q}));  // open: clr, load, up, D
  Pull_Resistor #(.pull(1)) pull_resistor_1 (.node(pull_resistor_1_node));
  // RGB_Video #(.height(256), .width(256)) rgb_video_1: pin names not known; wires that end beside it: counter_1_carry, clock_1_out, rgb_video_1_p3
  Pull_Resistor #(.pull(1)) pull_resistor_2 ();  // open: node
  RAM #(.addrWidth(16), .dataWidth(16)) ram_1 (
    .addr({counter_1_q_2, counter_1_q}), .oe(pull_resistor_3_node), .clk(clock_1_out),
    .din({counter_1_q_2, counter_1_q}), .dout(rgb_video_1_p3));  // open: we
  Pull_Resistor #(.pull(1)) pull_resistor_3 (.node(pull_resistor_3_node));
endmodule
