// Logisim project wackotron.circ as structural Verilog: 1 circuit, main circuit main
module main (
);

  wire keyboard_1_avail, rv32im_1_p1, socjtaguart_1_p1, socjtaguart_1_p2, socjtaguart_1_p3, socjtaguart_1_p4,
       socjtaguart_1_p7, socjtaguart_1_p8, socjtaguart_1_p12, socjtaguart_1_p13, socpio_1_p1, socpio_2_p1,
       socpio_2_p2, undriven_3, undriven_4, undriven_5, undriven_6, undriven_7;
  wire [6:0] keyboard_1_data, socjtaguart_1_p11;
  wire [19:0] undriven, undriven_2;
  wire [31:0] rom_1_data, rom_2_data;

  ROM #(.addrWidth(20), .dataWidth(32)) rom_1 (.addr(undriven), .data(rom_1_data));
  // SocPio #(.SocBusSelection('h0000017E0235E8FD14a1bb74), .StartAddress('h10000030), .direction("inout"), .width(32)) socpio_1: pin names not known; wires that end beside it: socpio_1_p1
  // Socmem #(.MemSize(12), .SocBusSelection('h0000017E0235E8FD14a1bb74)) socmem_1: pin names not known
  // Socmem #(.MemSize(26), .SocBusSelection('h0000017E0235E8FD14a1bb74), .StartAddress('h80000000)) socmem_2: pin names not known
  // Socmem #(.MemSize(26), .SocBusSelection('h0000017E0235E8FD14a1bb74), .StartAddress('h84000000)) socmem_3: pin names not known
  ROM #(.addrWidth(20), .dataWidth(32)) rom_2 (.addr(undriven_2), .data(rom_2_data));
  // SocPio #(.SocBusSelection('h0000017E0235E8FD14a1bb74), .StartAddress('h20000000), .direction("outputonly"), .width(32)) socpio_2: pin names not known; wires that end beside it: socpio_2_p1, socpio_2_p2
  // SocPio #(.SocBusSelection('h0000017E0235E8FD14a1bb74), .StartAddress('h10000000), .direction("inout"), .width(32)) socpio_3: pin names not known; wires that end beside it: socpio_1_p1
  LED led_1 (.in(socpio_2_p2));
  Clock clock_1 (.out(socpio_2_p1));
  LED led_2 (.in(undriven_3));
  LedBar ledbar_1 (
    .led0(undriven_4), .led1(undriven_5), .led2(undriven_6), .led3(undriven_7), .led4(socjtaguart_1_p1),
    .led5(socjtaguart_1_p2), .led6(socjtaguart_1_p3), .led7(socjtaguart_1_p4));
  // SocBus #(.SocBusIdentifier('h0000017E0235E8FD14a1bb74), .TraceSize(8)) socbus_1: pin names not known; wires that end beside it: socpio_1_p1
  // Rv32im #(.SocBusSelection('h0000017E0235E8FD14a1bb74), .exceptionVector('h100), .irqWidth(16), .resetVector('hfc0)) rv32im_1: pin names not known; wires that end beside it: rv32im_1_p1
  Button button_1 (.out(socpio_1_p1));
  // SocVga #(.BufferAddress('h80000000), .SocBusSelection('h0000017E0235E8FD14a1bb74), .StartAddress('h21000000)) socvga_1: pin names not known; wires that end beside it: socpio_1_p1, socpio_2_p1
  Keyboard keyboard_1 (
    .clk(socpio_2_p1), .re(socjtaguart_1_p7), .clr(socjtaguart_1_p8), .avail(keyboard_1_avail),
    .data(keyboard_1_data));
  // SocJtagUart #(.SocBusSelection('h0000017E0235E8FD14a1bb74), .StartAddress('h10000048)) socjtaguart_1: pin names not known; wires that end beside it: socjtaguart_1_p1, socjtaguart_1_p2, socjtaguart_1_p3, socjtaguart_1_p4, socpio_1_p1, socpio_2_p1, socjtaguart_1_p7, socjtaguart_1_p8, keyboard_1_avail, keyboard_1_data, socjtaguart_1_p11, socjtaguart_1_p12, socjtaguart_1_p13
  TTY #(.cols(50), .rows(20)) tty_1 (
    .data(socjtaguart_1_p11), .clk(socpio_2_p1), .we(socjtaguart_1_p12), .clr(socjtaguart_1_p13));

  // Notes on the sheet:
  //   contents of rom_1 (hex, n*v repeats v):
  //   f1402573 84ae822a 193 77297 6982a283 30529073 30401073 546342a1 42a11c52 3042a073 33752c1 71338020
  //   850a0053 2a00e0ef 1293842a 13300e2 ef4055 72976970 a2830007 43057a22 862a92f 91e63 2880e0ef e91a023
  //   c41ac23 77297 4782a283 a02a02f 77297 46c2a283 a32f4305 1ee30c62 81a2fe03 13334305 a3830043 e3b316c1
  //   a6230063 a02f1671 1e630a02 10ef1409 10ef0ce0 5130cc0 7f170000 2f030007 9f0265ef 89ae892a 12938a32
  //   13300e2 72974059 a2830007 fb356e2 8663405a 83520b42 77e17 5c8e2e03 405e0e33 1c283b3 2af03 20230291
  //   31101e3 fe72cae3 77317 39032303 77397 6b03a383 6730b63 93fe937e 2f03a8a9 4e0dff83 1cf1b63 ff432e03
  //   ffc32f03 9e7e9f7e 1ee2023 7e97a83d ae830007 9efe686e ff832f03 8f5293 fff7f13 12634e05 2e0303cf
  //   4f41ff43 3e282b3 5e8ab3 ffc32283 4aaf03 9f7e9f16 20239e7e 33101ee fa63d3e3 77297 5382a283 907392fe
  //   72973052 a2830007 92fe5222 77317 40c32303 8763937e a0230062 2910002 fe62cde3 77297 2bc2a283 1f28533
  //   85ca8afe 693864e 10ef0000 c9112ce0 751785aa 25030007 ef29a5 d0ef3205 8fd678c4 75d000ef 75f000ef
  //   77297 3d42a283 1f28eb3 85d2854e 738e82 bff51050 e21293 40558133 7381b2 22f31050 f2933440 8ae30082
  //   8512fe02 20a010ef ffffb7ed 5378082 50d8000 5378082 50d8000 5378082 50d8000 5378082 50d8000 5378082
  //   50d8000 5378082 50d8000 5378082 50d8000 17178082 7130000 431cb667 c5adc3b5 e6894194 c12d8905
  //   80824501 472303 872e03 16634501 53700a3 5398000 47d88082 87a803 e863eb0d 4f980306 58934fd0 6320147
  //   e6330732 8b300c8 b7330107 973200e8 f863e319 4b9c0116 86b396be c1944106 505bf45 bf6597f2 80000537
  //   8082050d 80000537 80820509 c4221141 4550c606 2823842a 85aa0005 25194501 c80840b2 1414422 47818082
  //   f61363 87338082 468300f5 7330007 78500f5 d70023 7517b7e5 25030007 77972165 a7830007 c13c3567 77797
  //   2647a783 7797cd1c a7830007 cd5c28e7 7179b745 d04ad226 4b7ce4e 79178000 29030007 79971e29 a9830007
  //   d42240a9 ca56cc52 c65ec85a c266c462 8c2ed606 77c97 180cac83 77a17 2b4a2a03 77a97 448aaa83 950433
  //   1890b13 498b93 34ce063 50b25422 59025492 4a6249f2 4b424ad2 4c224bb2 61454c92 5910006f 401a783 ca503
  //   953e97a6 c0c63 1656663 4c90793 8a7f863 8ab8663 8a98463 4ca783 f6134705 d630ff7 478d04e6 4f61f63
  //   8ca683 76396a2 2783060c 2703014c e39d010c 2e6e263 18c2783 1cc2603 147d593 63207b2 8e4d973e f737b3
  //   e3a997b2 4d77063 8597862a 85930005 517fb65 5130000 ef5025 a00d0c45 79283a1 43d497d6 4681b775 58597
  //   f9458593 517 4bc50513 a2500ef bf1d0cb1 8350593 f593c114 7513f805 eff805 b7ed4db0 c4221141 84324781
  //   22c1c606 401cc409 7f7f793 40b2c01c 1414422 a2058082 4701882a 7b34e41 c30300e8 87b30107 c88300e5
  //   7050007 411307b3 17b513 1c70563 ff1301e3 7134501 55830208 c5110007 65783 b5138f8d 7090017 609c199
  //   c699b7ed 82783 973e079d c2989b61 1797c509 af230000 80829307 15971141 85930000 45019365 3385c606
  //   179740b2 a1230000 1419207 71798082 d226d422 d04ad606 cc52ce4e 1497ca56 84930000 40dc9064 5d703
  //   a9038432 993e0107 ee01e705 50b24481 59025422 4a6249f2 85264ad2 61455492 7e18082 e3e3c21c 2023ff27
  //   bff90004 40888a2a cd1189ae 862e86b2 371d85d2 c411c909 e463401c 20230127 40840004 40c4bf7d f46304e1
  //   a930324 86d600c1 85d2864e 3dfd8526 e36347b2 c6020127 dc51c509 c01c47b2 44b2bf59 f455f0ed ed11b771
  //   80000537 80820509 80000537 40f20509 44d24462 61054942 11018082 ce06cc22 c84aca26 d1ed842e de798932
  //   84aa410c 2c3d8522 9e3409c 70fcf5 854a85a2 e5013f39 45783 45b2f3e1 8593c59d 87ae0205 7d703 ff6d0789
  //   86334098 c09040b7 c76f63 31c58522 854a45b2 5c14641 450139d9 537bf59 5398000 537b779 5158000 882ab759
  //   537ed19 5098000 5378082 5098000 446240f2 494244d2 610549b2 852e8082 1101d1ed ce06cc22 c84aca26
  //   8436c64e 89b2dee9 460185c2 893e84ba cd153d59 98563 a023415c 86300f9 45180009 2023455c 222300e9
  //   411000f9 c010401c 2c7e163 593d0dd d7830205 5890005 8526ffed 450131a9 537bf61 5398000 537bf41 5158000
  //   cd31b761 c4221141 417c606 4130000 40587564 4b1c4014 f70633 a6e663 697 7406a023 2050593 5d683
  //   feed0589 97aa4114 95b6069d 8f8d99e1 cb1c8e0d 40403ecd 48104501 1840593 2af91621 40b2c848 1414422
  //   80828082 c4627139 c17 6fcc0c13 2883de46 d226004c ca56d04a c65ec85a d422d606 cc52ce4e a403c266
  //   893e0108 84b68aaa 8b428bba 47819446 179993 13a8733 75703 fb6d0785 2040c93 8b30989 8a334119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
  //   Bootloader PROM
  //   contents of rom_2 (hex, n*v repeats v):
  //   e1364d42 0 360000 280000 a00000 780000 10000 18 e1000000 ec40000 ec40000 0 0 0 1010100 1000000 101
  //   1010100 1000000 1010101 1 1000000 101 1010100 1010101 1010101 1010101 10101 1010000 1 1010101 101
  //   1010000 2000000 30101 0 1000000 2030101 202 1010100 101 1010200 3010103 1030000 1010001 10101
  //   1010000 1010101 10101 1030000 1010301 1010103 1000202 1010101 1010101 2040101 1020402 11010102
  //   2c281d11 4c3b353a 3c5e504c 302b5240 67544d44 5f7a6158 87798367 ae96899d 81b09f90 8f78a693 bca590a5
  //   81b4a092 9a8ba691 c4ad98b0 90b8a794 988cb8a5 baa493af 91b9a195 9385b1a0 aa9287a8 7faa9584 8379a387
  //   907d6d9d 679e8977 5f548f77 9176687a 6b877263 59548770 3b29276f 4120809 2030502 3030502 2020203
  //   3050303 1010403 2020201 2020202 2 2010101 202 0 1010101 1010101 1 1020202 101 0 10101 0 1010100 0
  //   1010000 1 1000000 101 1010100 1000000 101 1010100 0 1010000 1 10101 1010000 1010101 10101 0 1010100
  //   1000000 1010101 1010101 1010101 101 1010100 1010101 1010101 1 10101 0 1010100 1000000 101 0 1010101
  //   2020101 2 0 0 1010100 10101 1000101 1 10101 0 200 4010104 20101 1010100 1010101 1000101 1010001
  //   10100 1010000 2020201 0 0 1010100 1000000 1010101 1 10101 0 1010100 5020201 1040303 3030201 5030303
  //   2040203 e060805 2c261618 38304330 67534a4d 446c5652 504f543f 96847564 92a19079 a28db19f bca793b8
  //   a3c3b19c b4a1cab6 d0bfadc7 9fd4c8b5 bdb0bdb0 c6baa6ce a7c7b6a0 a595c7b4 bea498ba a7b49c8f 9988c8b7
  //   bdaa9aa9 72bca798 86799380 ab9a8b9f 86bfafa1 6157a993 8b6b617d 789f8379 625b987e 725e5777 b3a2a26
  //   305150a 6040406 2020302 3030302 2020103 1010101 101 1010100 1000000 101 0 10101 0 1010100 1010101
  //   101 2020200 1010101 1010101 1 1000000 1010101 1 10101 1010000 1 1010101 1010101 1 10101 1010000
  //   1010101 1000000 1010101 1 1010101 101 1010100 1010101 101 0 0 1010000 1010101 1010101 101 1010100 0
  //   1010000 1 10100 0 1010100 1000000 1010101 1010101 1010101 101 1010100 3000000 10000 0 10101 1010000
  //   101 1010101 1010000 1010101 10101 1020000 201 2000002 0 1010100 2000000 1040101 1 1000000 2020101 2
  //   1000000 101 1010100 3030303 3030202 2020203 4030403 a0b0301 27191c11 4756483f 4e49614e 70575264
  //   535d4545 77706953 a5958389 8db6a68e b09eb59f c2a999c3 9fb0988d b3a2c1ac bfac9dc6 bac9b7a6 e0d1d3cc
  //   e3d8c7e6 b9ded3c2 c6b6d5c7 c4b3a2d7 9ebcaa9a 9a87bfb0 beab9baf 8bc1b19f 807daf96 ac99899d 9da69685
  //   a495bcaa 87756ab4 7b876d60 7872a181 8c706a96 245f4240 90a3822 f0b0b16 5040405 4040303 2020304
  //   3030305 2020202 2020202 1000000 101 0 10101 1010000 1 1000000 1010101 1 1010101 1010101 1010101
  //   1000000 1010101 1 10101 1010000 1010101 1000000 101 1010100 10101 1010000 4*1010101 10101 1010000
  //   1010101 1010101 101 0 10101 1010000 1 1010101 101 2020200 10101 1010000 1010201 1010102 101 0
  //   1000000 101 1010100 10101 1000000 101 2000001 1020101 1 1000000 101 0 10101 1010000 1010101 2010101
  //   1020101 1010201 2010102 1010000 1010101 2000000 1020101 1010001 20202 1010000 1 2020202 1010202
  //   2020101 1030202 2020101 4030302 4030303 27260905 4e3b3835 484d3933 675f634e 68554d7a 70725d57
  //   83788f77 ac948598 8eb6a694 9f8cb3a1 b29a86b5 82b49a8e bcaea68d dccbbccf dee1d4c2 ede2f7f1 e2e0cef5
  //   bee7dcc7 d1bedad0 d9ccbfd9 a7d8d1c0 a698c8b4 beac9cb8 87c0aa9c 918baf97 bca79bae 8fbda99c a799b3a1
  //   aa9289b9 76ac8f83 776b9a81 947b6d90 497c5f57 1918644c 160a0a2c 31d1a1c 2030101 4030303 3020203
  //   2020303 1010102 20202 0 1010100 2010101 2020202 2 1010101 2020101 1010102 1010101 2020101 1010102
  //   4*1010101 101 0 10101 1010000 1010101 0 0 1010100 1000000 101 1010100 1000000 101 1010100 0 1020000
  //   1010101 1000000 1010101 1 0 0 1010100 1000000 101 1010300 1010102 101 0 1010101 101 0 10101 1000000
  //   301 1010103 2010202 2 3010101 1010202 1 20202 3030000 1010103 4020203 1020202 1 2010102 1010101
  //   1010101 1020201 0 1010100 1010101 1010101 1010101 2020202 2020202 3020302 2030102 2030302 6050603
  //   19080404 3d3b291a 57463f50 4b644f4f 58556549 8d77716f 7d89756a 9e929f89 b7a596af 99a99588 a092bba5
  //   b49a8cb9 acb8a395 b3a6c9ba dac6b6c8 c9d9c9b8 f1dae9df eae1d0f3 d5e7e6d3 d8c6f2e7 d0cbbbe5 c9eae5d7
  //   b5a9e2d4 b49f90ca 8bc9aea1 aca2b294 b09b89cb a9c8b0a2 a594c9b6 b09285b8 95af897e 958cb39b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
  //   External PROM
endmodule
